// Logisim project Alu.circ as structural Verilog: 2 circuits, main circuit ALU
module ALU (
  input  [3:0] codeOP,
  input  [4:0] shifter,
  input  Cin,
  input  [31:0] A,
  input  [31:0] B,
  output [31:0] OUT,
  output ZERO,
  output NEGATIVE,
  output OVERFLOW,
  output CARRY_OUT
);

  wire A_t, adder_1_cout, adder_2_cout, B_t, RESULT, subtractor_1_bout, subtractor_2_bout, subtractor_3_bout;
  wire [31:0] adder_1_out, adder_2_out, and_2_out, and_3_out, AND_out, EOR_out, multiplier_1_out, not_1_out,
       not_2_out, or_1_out, shifter_1_out, shifter_2_out, shifter_3_out, shifter_4_out, subtractor_1_out,
       subtractor_2_out, subtractor_3_out;

  Subtractor #(.width(32)) subtractor_1 (.a(B), .b(A), .out(subtractor_1_out), .bin(Cin), .bout(subtractor_1_bout));
  assign not_1_out = ~B;  // NOT_Gate not_1, 32 bits wide
  BitSelector #(.width(32)) bitselector_1 (.in(B), .out(B_t), .sel({5{1'b1}}));
  BitSelector #(.width(32)) bitselector_2 (.in(A), .out(A_t), .sel({5{1'b1}}));
  assign AND_out = A & B;  // AND_Gate AND, 32 bits wide
  assign EOR_out = A ^ B;  // XOR_Gate EOR, 32 bits wide
  Shifter #(.width(32)) shifter_1 (.in(A), .\dist (shifter), .out(shifter_1_out));
  Shifter #(.width(32), .shift("lr")) shifter_2 (.in(A), .\dist (shifter), .out(shifter_2_out));
  Shifter #(.width(32), .shift("ar")) shifter_3 (.in(A), .\dist (shifter), .out(shifter_3_out));
  Adder #(.width(32)) adder_1 (.a(A), .b(B), .out(adder_1_out), .cin(Cin), .cout(adder_1_cout));
  Shifter #(.width(32), .shift("rr")) shifter_4 (.in(A), .\dist (shifter), .out(shifter_4_out));
  assign and_2_out = A & B;  // AND_Gate and_2, 32 bits wide
  Subtractor #(.width(32)) subtractor_2 (
    .a({32{1'b0}}), .b(B), .out(subtractor_2_out), .bout(subtractor_2_bout));  // open: bin
  Subtractor #(.width(32)) subtractor_3 (.a(B), .b(A), .out(subtractor_3_out), .bout(subtractor_3_bout));  // open: bin
  Adder #(.width(32)) adder_2 (.a(A), .b(B), .out(adder_2_out), .cout(adder_2_cout));  // open: cin
  assign or_1_out = A | B;  // OR_Gate or_1, 32 bits wide
  Multiplier #(.width(32)) multiplier_1 (.a(A), .b(B), .out(multiplier_1_out));  // open: cin, cout
  assign and_3_out = A & not_1_out;  // AND_Gate and_3, 32 bits wide
  assign not_2_out = ~B;  // NOT_Gate not_2, 32 bits wide
  Multiplexer #(.select(4), .width(32), .enable("false")) multiplexer_1 (
    .in0(AND_out), .in1(EOR_out), .in2(shifter_1_out), .in3(shifter_2_out), .in4(shifter_3_out),
    .in5(adder_1_out), .in6(subtractor_1_out), .in7(shifter_4_out), .in8(and_2_out), .in9(subtractor_2_out),
    .in10(subtractor_3_out), .in11(adder_2_out), .in12(or_1_out), .in13(multiplier_1_out), .in14(and_3_out),
    .in15(not_2_out), .out(OUT), .sel(codeOP));
  BitSelector #(.width(32)) bitselector_3 (.in(OUT), .out(RESULT), .sel({5{1'b1}}));
  Multiplexer #(.select(4), .enable("false")) multiplexer_2 (
    .in0(1'b0), .in1(1'b0), .in2(1'b0), .in3(1'b0), .in4(1'b0), .in5(adder_1_cout), .in6(subtractor_1_bout),
    .in7(1'b0), .in8(1'b0), .in9(subtractor_2_bout), .in10(subtractor_3_bout), .in11(adder_2_cout),
    .in12(1'b0), .in13(1'b0), .in14(1'b0), .in15(1'b0), .out(CARRY_OUT), .sel(codeOP));
  Comparator #(.width(32)) comparator_1 (.a(OUT), .b({32{1'b0}}), .eq(ZERO), .lt(NEGATIVE));  // open: gt
  OverFlowDetector overflowdetector_1 (.A31(A_t), .B31(B_t), .R31(RESULT), .OverFlow(OVERFLOW), .CODEOP(codeOP));

  // Other names for the same wires on the sheet: CodeOPP[3:0] = codeOP
endmodule

module OverFlowDetector (
  input  [3:0] CODEOP,
  input  A31,
  input  B31,
  input  R31,
  output OverFlow
);

  wire ADD, and_1_out, and_2_out, and_3_out, and_4_out, and_5_out, and_6_out, and_7_out, and_8_out,
       comparator_1_eq, comparator_2_eq, comparator_3_eq, comparator_4_eq, not_1_out, not_2_out, not_3_out,
       not_4_out, not_5_out, not_6_out, not_7_out, or_3_out, or_4_out, SUB, SUB0;

  Comparator #(.width(4)) comparator_1 (.a(CODEOP), .b(4'b0110), .eq(comparator_1_eq));  // open: gt, lt
  Comparator #(.width(4)) comparator_2 (.a(CODEOP), .b(4'b1010), .eq(comparator_2_eq));  // open: gt, lt
  Comparator #(.width(4)) comparator_3 (.a(CODEOP), .b(4'b0101), .eq(comparator_3_eq));  // open: gt, lt
  Comparator #(.width(4)) comparator_4 (.a(CODEOP), .b(4'b1011), .eq(comparator_4_eq));  // open: gt, lt
  Comparator #(.width(4)) comparator_5 (.a(CODEOP), .b(4'b1001), .eq(SUB0));  // open: gt, lt
  not not_1 (not_1_out, A31);
  or or_1 (SUB, comparator_1_eq, comparator_2_eq);
  not not_2 (not_2_out, R31);
  not not_3 (not_3_out, A31);
  not not_4 (not_4_out, B31);
  not not_5 (not_5_out, B31);
  not not_6 (not_6_out, R31);
  not not_7 (not_7_out, 1'b0);
  or or_2 (ADD, comparator_3_eq, comparator_4_eq);
  and and_1 (and_1_out, A31, not_2_out, B31);
  and and_2 (and_2_out, not_3_out, R31, not_4_out);
  and and_3 (and_3_out, A31, R31, not_5_out);
  and and_4 (and_4_out, not_1_out, not_6_out, B31);
  and and_5 (and_5_out, B31, R31, not_7_out);
  or or_3 (or_3_out, and_1_out, and_2_out);
  or or_4 (or_4_out, and_3_out, and_4_out);
  and and_6 (and_6_out, ADD, or_3_out);
  and and_7 (and_7_out, SUB, or_4_out);
  and and_8 (and_8_out, SUB0, and_5_out);
  or or_5 (OverFlow, and_6_out, and_7_out, and_8_out);

  // Other names for the same wires on the sheet: A = A31; B = B31; R = R31
endmodule
