// Logisim project AluBancRegistre.circ as structural Verilog: 2 circuits, main circuit banc de registre
module banc_de_registre (
  input  [31:0] DataIn,
  input  clock,
  input  Reset,
  input  [2:0] RegA,
  input  [3:0] regdest,
  input  [2:0] RegB,
  output [31:0] Aout,
  output [31:0] Bout
);

  wire decoder_1_out0, decoder_1_out1, decoder_1_out2, decoder_1_out3, decoder_1_out4, decoder_1_out5,
       decoder_1_out6, decoder_1_out7;
  wire [31:0] register_1_q, register_2_q, register_3_q, register_4_q, register_5_q, register_6_q,
       register_7_q, register_8_q;

  Decoder #(.select(4), .enable("false")) decoder_1 (
    .out0(decoder_1_out0), .out1(decoder_1_out1), .out2(decoder_1_out2), .out3(decoder_1_out3),
    .out4(decoder_1_out4), .out5(decoder_1_out5), .out6(decoder_1_out6), .out7(decoder_1_out7), .sel(regdest));  // open: out8, out9, out10, out11, out12, out13, out14, out15
  Register #(.width(32), .trigger("falling")) register_1 (
    .D(DataIn), .en(decoder_1_out0), .Q(register_1_q), .clk(clock), .clr(Reset));
  Register #(.width(32), .trigger("falling")) register_2 (
    .D(DataIn), .en(decoder_1_out1), .Q(register_2_q), .clk(clock), .clr(Reset));
  Register #(.width(32), .trigger("falling")) register_3 (
    .D(DataIn), .en(decoder_1_out2), .Q(register_3_q), .clk(clock), .clr(Reset));
  Register #(.width(32), .trigger("falling")) register_4 (
    .D(DataIn), .en(decoder_1_out3), .Q(register_4_q), .clk(clock), .clr(Reset));
  Register #(.width(32), .trigger("falling")) register_5 (
    .D(DataIn), .en(decoder_1_out4), .Q(register_5_q), .clk(clock), .clr(Reset));
  Register #(.width(32), .trigger("falling")) register_6 (
    .D(DataIn), .en(decoder_1_out5), .Q(register_6_q), .clk(clock), .clr(Reset));
  Register #(.width(32), .trigger("falling")) register_7 (
    .D(DataIn), .en(decoder_1_out6), .Q(register_7_q), .clk(clock), .clr(Reset));
  Register #(.width(32), .trigger("falling")) register_8 (
    .D(DataIn), .en(decoder_1_out7), .Q(register_8_q), .clk(clock), .clr(Reset));
  Multiplexer #(.select(3), .width(32), .enable("false")) multiplexer_1 (
    .in0(register_1_q), .in1(register_2_q), .in2(register_3_q), .in3(register_4_q), .in4(register_5_q),
    .in5(register_6_q), .in6(register_7_q), .in7(register_8_q), .out(Aout), .sel(RegA));
  Multiplexer #(.select(3), .width(32), .enable("false")) multiplexer_2 (
    .in0(register_1_q), .in1(register_2_q), .in2(register_3_q), .in3(register_4_q), .in4(register_5_q),
    .in5(register_6_q), .in6(register_7_q), .in7(register_8_q), .out(Bout), .sel(RegB));
endmodule

// Unité de Calcul
module CalculUnit (
  input  [31:0] DataIn_From_Ram,
  input  [7:0] DataIn_From_Imm8,
  input  LoadImm8,
  input  DATAinSelecter,
  input  RESET,
  input  clock,
  input  [3:0] REGDEST,
  input  [2:0] REGa,
  input  [3:0] CODOP,
  input  [2:0] REGb,
  input  [4:0] SHIFTER,
  input  ShiftFromRegister,
  input  Cin,
  output [31:0] DataOut_TO_Ram,
  output [3:0] Flags
);

  wire [4:0] FinalShifter, ShifterFromRegister;
  wire [31:0] banc_de_registre_1_aout, bit_extender_1_out, DataToLoad, multiplexer_3_out, OperationResult;

  Multiplexer #(.width(5), .enable("false")) multiplexer_1 (
    .in0(SHIFTER), .in1(ShifterFromRegister), .out(FinalShifter), .sel(ShiftFromRegister));
  assign bit_extender_1_out = {{24{DataIn_From_Imm8[7]}}, DataIn_From_Imm8};  // Bit_Extender bit_extender_1
  // Probe on bit_extender_1_out
  Multiplexer #(.width(32), .enable("false")) multiplexer_2 (
    .in0(DataIn_From_Ram), .in1(bit_extender_1_out), .out(DataToLoad), .sel(LoadImm8));
  Multiplexer #(.width(32), .enable("false")) multiplexer_3 (
    .in0(OperationResult), .in1(DataToLoad), .out(multiplexer_3_out), .sel(DATAinSelecter));
  banc_de_registre banc_de_registre_1 (
    .DataIn(multiplexer_3_out), .RegA(REGa), .regdest(REGDEST), .RegB(REGb), .Reset(RESET),
    .Aout(banc_de_registre_1_aout), .Bout(DataOut_TO_Ram), .clock(clock));
  BitSelector #(.width(32), .group(5)) bitselector_1 (.in(DataOut_TO_Ram), .out(ShifterFromRegister), .sel(3'b000));
  ALU alu_1 (
    .codeOP(CODOP), .shifter(FinalShifter), .Cin(Cin), .A(banc_de_registre_1_aout), .B(DataOut_TO_Ram),
    .OUT(OperationResult), .ZERO(Flags[0]), .NEGATIVE(Flags[1]), .CARRY_OUT(Flags[3]), .OVERFLOW(Flags[2]));

  // Other names for the same wires on the sheet: ClockReg = clock; CodeOp[3:0] = CODOP; DataSel = DATAinSelecter;
  //   ResetReg = RESET
endmodule
