// Logisim project Controler.circ as structural Verilog
module Controller (
  input  [3:0] Flags,
  input  clock,
  input  reset,
  input  [15:0] inst,
  output [7:0] Program_Counter,
  output shiftFromRegistrer,
  output DataSelector,
  output [1:0] Load_Store,
  output [3:0] Codeop,
  output [2:0] Rm,
  output [2:0] Rn,
  output [3:0] Rd,
  output [4:0] Imm5,
  output [7:0] Imm8,
  output LoadImm8,
  output CarryValue
);

  wire CarryUseMod, LdrStr, multiplexer_1_out, multiplexer_2_out, multiplexer_3_out, multiplexer_14_out,
       multiplexer_16_out, multiplexer_22_out, not_1_out;
  wire [1:0] CatSelCod, SousCatASelCod, SousCatBSelCod;
  wire [2:0] multiplexer_5_out, multiplexer_6_out, multiplexer_7_out, multiplexer_8_out, multiplexer_9_out,
       multiplexer_10_out, R2_0, R5_3, R8_6, R10_8;
  wire [3:0] bit_extender_1_out, bit_extender_2_out, bit_extender_3_out, CodOpA, CodOpB, cond, flags_t,
       multiplexer_4_out, multiplexer_11_out, multiplexer_12_out;
  wire [4:0] imm5_t, multiplexer_13_out;
  wire [7:0] imm8_t, multiplexer_15_out;
  wire [15:0] Registre_d_instruction_q;

  ProgramCounter programcounter_1 (
    .Reset(reset), .Clock(clock), .CategorieCode(CatSelCod), .BanchAdress(imm8_t), .ConditionCode(cond),
    .Flags(flags_t), .Program_Counter(Program_Counter));
  Register #(.width(16)) Registre_d_instruction (
    .D(inst), .Q(Registre_d_instruction_q), .clk(clock), .clr(reset));  // open: en
  Register #(.width(4), .trigger("falling")) u_Flags (.D(Flags), .Q(flags_t), .clk(clock), .clr(reset));  // open: en
  // Probe on CatSelCod
  CategorieDecoder categoriedecoder_1 (
    .Instruction(Registre_d_instruction_q), .categorie_select_code(CatSelCod),
    .Sous_Categorie_A_Select_code(SousCatASelCod), .Sous_Categorie_B_Select_code(SousCatBSelCod));
  CodOpDecoder codopdecoder_1 (.in_1(Registre_d_instruction_q), .CodOpB(CodOpB), .CodOpA(CodOpA));
  OperandDecoder operanddecoder_1 (
    .in_1(Registre_d_instruction_q), .R2_0(R2_0), .R5_3(R5_3), .R8_6(R8_6), .Rd10_8(R10_8), .Imm5(imm5_t),
    .Imm8(imm8_t), .LoadStoreSignal(LdrStr), .Condition(cond), .CarryUseMod(CarryUseMod));
  Multiplexer #(.select(2), .enable("false")) multiplexer_1 (
    .in0(1'b0), .in1(1'b0), .in2(1'b1), .in3(1'b0), .out(multiplexer_1_out), .sel(SousCatASelCod));
  assign bit_extender_1_out = {{1{1'b0}}, R2_0};  // Bit_Extender bit_extender_1
  Multiplexer #(.select(2), .enable("false")) multiplexer_2 (
    .in0(1'b1), .in1(1'b0), .in2(1'b0), .in3(1'b0), .out(multiplexer_2_out), .sel(SousCatBSelCod));
  Multiplexer #(.enable("false")) multiplexer_3 (.in0(1'b0), .in1(1'b1), .out(multiplexer_3_out), .sel(LdrStr));
  Multiplexer #(.select(2), .width(4), .enable("false")) multiplexer_4 (
    .in0(CodOpA), .in1(CodOpA), .out(multiplexer_4_out), .sel(SousCatASelCod));  // open: in2, in3
  Multiplexer #(.select(2), .width(3), .enable("false")) multiplexer_5 (
    .in0(R5_3), .in1(R8_6), .out(multiplexer_5_out), .sel(SousCatASelCod));  // open: in2, in3
  Multiplexer #(.select(2), .width(3), .enable("false")) multiplexer_6 (
    .in0(R5_3), .in1(R5_3), .in3(R2_0), .out(multiplexer_6_out), .sel(SousCatBSelCod));  // open: in2
  Multiplexer #(.select(2), .width(3), .enable("false")) multiplexer_7 (
    .in1(R5_3), .out(multiplexer_7_out), .sel(SousCatASelCod));  // open: in0, in2, in3
  Multiplexer #(.select(2), .width(3), .enable("false")) multiplexer_8 (
    .in0(R2_0), .in1(R2_0), .in2(R5_3), .in3(R5_3), .out(multiplexer_8_out), .sel(SousCatBSelCod));
  Multiplexer #(.width(3), .enable("false")) multiplexer_9 (
    .in0(R10_8), .out(multiplexer_9_out), .sel(LdrStr));  // open: in1
  Multiplexer #(.select(2), .width(3), .enable("false")) multiplexer_10 (
    .in0(R2_0), .in1(R2_0), .in2(R10_8), .out(multiplexer_10_out), .sel(SousCatASelCod));  // open: in3
  Multiplexer #(.select(2), .width(4), .enable("false")) multiplexer_11 (
    .in0(bit_extender_1_out), .in1(4'b1111), .in2(bit_extender_1_out), .in3(bit_extender_1_out),
    .out(multiplexer_11_out), .sel(SousCatBSelCod));
  Multiplexer #(.width(4), .enable("false")) multiplexer_12 (
    .in0(4'b1111), .in1(bit_extender_2_out), .out(multiplexer_12_out), .sel(LdrStr));
  assign bit_extender_2_out = {{1{1'b0}}, R10_8};  // Bit_Extender bit_extender_2
  Multiplexer #(.select(2), .width(5), .enable("false")) multiplexer_13 (
    .in0(imm5_t), .out(multiplexer_13_out), .sel(SousCatASelCod));  // open: in1, in2, in3
  not not_1 (not_1_out, flags_t[3]);
  Multiplexer #(.enable("false")) multiplexer_14 (
    .in0(not_1_out), .in1(flags_t[3]), .out(multiplexer_14_out), .sel(CarryUseMod));
  // Probe on CodOpB
  Multiplexer #(.select(2), .width(8), .enable("false")) multiplexer_15 (
    .in2(imm8_t), .out(multiplexer_15_out), .sel(SousCatASelCod));  // open: in0, in1, in3
  Multiplexer #(.select(2), .enable("false")) multiplexer_16 (
    .in0(1'b0), .in1(1'b0), .in2(1'b1), .in3(1'b0), .out(multiplexer_16_out), .sel(SousCatASelCod));
  Multiplexer #(.select(2), .enable("false")) multiplexer_17 (
    .in0(1'b0), .in1(multiplexer_2_out), .in2(1'b0), .in3(1'b0), .out(shiftFromRegistrer), .sel(CatSelCod));
  Multiplexer #(.select(2), .enable("false")) multiplexer_18 (
    .in0(multiplexer_1_out), .in1(1'b0), .in2(multiplexer_3_out), .in3(1'b0), .out(DataSelector),
    .sel(CatSelCod));
  Multiplexer #(.select(2), .width(4), .enable("false")) multiplexer_19 (
    .in0(multiplexer_4_out), .in1(CodOpB), .out(Codeop), .sel(CatSelCod));  // open: in2, in3
  Multiplexer #(.select(2), .width(3), .enable("false")) multiplexer_20 (
    .in0(multiplexer_5_out), .in1(multiplexer_6_out), .out(Rm), .sel(CatSelCod));  // open: in2, in3
  assign bit_extender_3_out = {{1{1'b0}}, multiplexer_10_out};  // Bit_Extender bit_extender_3
  Multiplexer #(.select(2), .enable("false")) multiplexer_21 (
    .in0(multiplexer_16_out), .in1(1'b0), .in2(1'b0), .in3(1'b0), .out(LoadImm8), .sel(CatSelCod));
  Multiplexer #(.select(2), .enable("false")) multiplexer_22 (
    .in0(multiplexer_14_out), .out(multiplexer_22_out), .sel(SousCatBSelCod));  // open: in1, in2, in3
  Multiplexer #(.select(2), .width(2), .enable("false")) multiplexer_23 (
    .in0(2'b00), .in1(2'b00), .in2({LdrStr, 1'b1}), .in3(2'b00), .out(Load_Store), .sel(CatSelCod));
  Multiplexer #(.select(2), .width(3), .enable("false")) multiplexer_24 (
    .in0(multiplexer_7_out), .in1(multiplexer_8_out), .in2(multiplexer_9_out), .out(Rn), .sel(CatSelCod));  // open: in3
  Multiplexer #(.select(2), .width(4), .enable("false")) multiplexer_25 (
    .in0(bit_extender_3_out), .in1(multiplexer_11_out), .in2(multiplexer_12_out), .in3(4'b1111), .out(Rd),
    .sel(CatSelCod));
  Multiplexer #(.select(2), .width(5), .enable("false")) multiplexer_26 (
    .in0(multiplexer_13_out), .out(Imm5), .sel(CatSelCod));  // open: in1, in2, in3
  Multiplexer #(.select(2), .width(8), .enable("false")) multiplexer_27 (
    .in0(multiplexer_15_out), .in2(imm8_t), .out(Imm8), .sel(CatSelCod));  // open: in1, in3
  Multiplexer #(.select(2), .enable("false")) multiplexer_28 (
    .in1(multiplexer_22_out), .out(CarryValue), .sel(CatSelCod));  // open: in0, in2, in3

  // Other names for the same wires on the sheet: MainClock = clock; MainReset = reset
endmodule

// Categorie Decoder
module CategorieDecoder (
  input  [15:0] Instruction,
  output [1:0] categorie_select_code,
  output [1:0] Sous_Categorie_A_Select_code,
  output [1:0] Sous_Categorie_B_Select_code
);

  wire catdecoder_1_c0, catdecoder_1_c1, catdecoder_1_c2, catdecoder_1_c3, sousacategoriedecoder_1_s0,
       sousacategoriedecoder_1_s1, sousacategoriedecoder_1_s2, sousacategoriedecoder_1_s3,
       souscategoriebdecoder_1_c0, souscategoriebdecoder_1_c1, souscategoriebdecoder_1_c2,
       souscategoriebdecoder_1_c3;
  wire [1:0] priority_encoder_1_out, priority_encoder_3_out;

  CatDecoder catdecoder_1 (
    .b15(Instruction[15]), .b14(Instruction[14]), .b13(Instruction[13]), .b12(Instruction[12]),
    .b11(Instruction[11]), .b10(Instruction[10]), .c3(catdecoder_1_c3), .c2(catdecoder_1_c2),
    .c1(catdecoder_1_c1), .c0(catdecoder_1_c0));
  SousACategorieDecoder sousacategoriedecoder_1 (
    .b13(Instruction[13]), .S3(sousacategoriedecoder_1_s3), .b12(Instruction[12]),
    .S2(sousacategoriedecoder_1_s2), .b11(Instruction[11]), .S1(sousacategoriedecoder_1_s1),
    .b10(Instruction[10]), .S0(sousacategoriedecoder_1_s0));
  SousCategorieBDecoder souscategoriebdecoder_1 (
    .b9(Instruction[9]), .c3(souscategoriebdecoder_1_c3), .b8(Instruction[8]), .b7(Instruction[7]),
    .c2(souscategoriebdecoder_1_c2), .b6(Instruction[6]), .c1(souscategoriebdecoder_1_c1),
    .c0(souscategoriebdecoder_1_c0));
  Priority_Encoder #(.select(2)) priority_encoder_1 (
    .in0(sousacategoriedecoder_1_s0), .in1(sousacategoriedecoder_1_s1), .in2(sousacategoriedecoder_1_s2),
    .in3(sousacategoriedecoder_1_s3), .out(priority_encoder_1_out));  // open: gs, en_out, en_in
  Priority_Encoder #(.select(2)) priority_encoder_2 (
    .in0(catdecoder_1_c0), .in1(catdecoder_1_c1), .in2(catdecoder_1_c2), .in3(catdecoder_1_c3),
    .out(categorie_select_code));  // open: gs, en_out, en_in
  Priority_Encoder #(.select(2)) priority_encoder_3 (
    .in0(souscategoriebdecoder_1_c0), .in1(souscategoriebdecoder_1_c1), .in2(souscategoriebdecoder_1_c2),
    .in3(souscategoriebdecoder_1_c3), .out(priority_encoder_3_out));  // open: gs, en_out, en_in
  Multiplexer #(.select(2), .width(2), .enable("false")) multiplexer_1 (
    .in0(priority_encoder_1_out), .out(Sous_Categorie_A_Select_code), .sel(categorie_select_code));  // open: in1, in2, in3
  Multiplexer #(.select(2), .width(2), .enable("false")) multiplexer_2 (
    .in1(priority_encoder_3_out), .out(Sous_Categorie_B_Select_code), .sel(categorie_select_code));  // open: in0, in2, in3
endmodule

// CodeOp Decoder
module CodOpDecoder (
  input  [15:0] in_1,
  output [3:0] CodOpA,
  output [3:0] CodOpB
);

  CatAtoBDecoder catatobdecoder_1 (
    .b13(in_1[13]), .b12(in_1[12]), .b11(in_1[11]), .b10(in_1[10]), .b9(in_1[9]), .s3(CodOpA[3]),
    .s2(CodOpA[2]), .s1(CodOpA[1]), .s0(CodOpA[0]));

  assign CodOpB = in_1[9:6];
endmodule

// CatAtoB
module CatAtoBDecoder (
  input  b13,
  input  b12,
  input  b11,
  input  b10,
  input  b9,
  output s3,
  output s2,
  output s1,
  output s0
);

  wire and_1_out, and_2_out, and_3_out, and_4_out, and_5_out, and_6_out, and_7_out, and_8_out, not_1_out,
       not_2_out, not_3_out, not_4_out, not_5_out, not_6_out, not_7_out, not_8_out, not_9_out, not_10_out,
       not_11_out, not_12_out, not_13_out, not_14_out, not_15_out, not_16_out, not_17_out;

  not not_1 (not_1_out, b13);
  not not_2 (not_2_out, b11);
  not not_3 (not_3_out, b13);
  not not_4 (not_4_out, b10);
  not not_5 (not_5_out, b13);
  not not_6 (not_6_out, b12);
  not not_7 (not_7_out, b12);
  not not_8 (not_8_out, b11);
  not not_9 (not_9_out, b13);
  not not_10 (not_10_out, b10);
  not not_11 (not_11_out, b13);
  not not_12 (not_12_out, b12);
  not not_13 (not_13_out, b13);
  not not_14 (not_14_out, b10);
  not not_15 (not_15_out, b9);
  not not_16 (not_16_out, b12);
  not not_17 (not_17_out, b11);
  and and_1 (and_1_out, not_1_out, b12, not_2_out);
  and and_2 (and_2_out, not_3_out, b12, not_4_out);
  and and_3 (and_3_out, not_5_out, not_6_out);
  and and_4 (and_4_out, not_7_out, not_8_out);
  and and_5 (and_5_out, not_9_out, b11, not_10_out, b9);
  and and_6 (and_6_out, not_11_out, not_12_out, b11);
  and and_7 (and_7_out, not_13_out, b11, not_14_out, not_15_out);
  and and_8 (and_8_out, b13, not_16_out, not_17_out);
  or or_1 (s2, and_1_out, and_2_out);
  or or_2 (s1, and_3_out, and_4_out, and_5_out);
  or or_3 (s0, and_6_out, and_7_out, and_8_out);

  assign s3 = 1'b0;
endmodule

// Operand Decoder
module OperandDecoder (
  input  [15:0] in_1,
  output [2:0] R2_0,
  output [2:0] R5_3,
  output [2:0] R8_6,
  output [2:0] Rd10_8,
  output [4:0] Imm5,
  output [7:0] Imm8,
  output LoadStoreSignal,
  output [3:0] Condition,
  output CarryUseMod
);


  assign CarryUseMod = in_1[6];
  assign Condition = in_1[11:8];
  assign Imm5 = in_1[10:6];
  assign Imm8 = in_1[7:0];
  assign LoadStoreSignal = in_1[11];
  assign R2_0 = in_1[2:0];
  assign R5_3 = in_1[5:3];
  assign R8_6 = in_1[8:6];
  assign Rd10_8 = in_1[10:8];
endmodule

// Sous A categorie Decoder
module SousACategorieDecoder (
  input  b13,
  input  b12,
  input  b11,
  input  b10,
  output S3,
  output S2,
  output S1,
  output S0
);

  wire and_2_out, and_3_out, not_1_out, not_2_out, not_3_out, not_4_out, not_5_out, not_6_out, not_7_out,
       not_8_out;

  not not_1 (not_1_out, b12);
  and and_1 (S2, b13, not_1_out, not_2_out);
  not not_2 (not_2_out, b11);
  not not_3 (not_3_out, b13);
  not not_4 (not_4_out, b10);
  not not_5 (not_5_out, b13);
  and and_2 (and_2_out, not_5_out, not_6_out);
  not not_6 (not_6_out, b12);
  not not_7 (not_7_out, b13);
  and and_3 (and_3_out, not_7_out, not_8_out);
  not not_8 (not_8_out, b11);
  and and_4 (S1, not_3_out, b12, b11, not_4_out);
  or or_1 (S0, and_2_out, and_3_out);

  assign S3 = 1'b0;
endmodule

// InterCatDecoder
module CatDecoder (
  input  b15,
  input  b14,
  input  b13,
  input  b12,
  input  b11,
  input  b10,
  output c3,
  output c2,
  output c1,
  output c0
);

  wire not_1_out, not_2_out, not_3_out, not_4_out, not_5_out, not_6_out, not_7_out, not_8_out, not_9_out,
       not_10_out;

  not not_1 (not_1_out, b13);
  not not_2 (not_2_out, b14);
  not not_3 (not_3_out, b13);
  not not_4 (not_4_out, b15);
  not not_5 (not_5_out, b13);
  not not_6 (not_6_out, b12);
  not not_7 (not_7_out, b11);
  not not_8 (not_8_out, b10);
  not not_9 (not_9_out, b15);
  not not_10 (not_10_out, b14);
  and and_1 (c3, b15, b14, not_1_out, b12);
  and and_2 (c2, b15, not_2_out, not_3_out, b12);
  and and_3 (c1, not_4_out, b14, not_5_out, not_6_out, not_7_out, not_8_out);
  and and_4 (c0, not_9_out, not_10_out);
endmodule

// Program Counter
module ProgramCounter (
  input  Reset,
  input  Clock,
  input  [1:0] CategorieCode,
  input  [7:0] BanchAdress,
  input  [3:0] ConditionCode,
  input  [3:0] Flags,
  output [7:0] Program_Counter
);

  wire BranchBoolean;
  wire [7:0] adder_1_out, multiplexer_1_out, register_1_q;

  Adder adder_1 (.a(Program_Counter), .b(8'h1), .out(adder_1_out));  // open: cin, cout
  ConditionDecoder conditiondecoder_1 (
    .b3(ConditionCode[3]), .b2(ConditionCode[2]), .b1(ConditionCode[1]), .b0(ConditionCode[0]),
    .Zero(Flags[0]), .OverFlow(Flags[2]), .Negative(Flags[1]), .CarryOut(Flags[3]),
    .BanchingBoolean(BranchBoolean));
  Register register_1 (.D(adder_1_out), .Q(register_1_q), .clk(Clock), .clr(Reset));  // open: en
  Multiplexer #(.width(8), .enable("false")) multiplexer_1 (
    .in0(register_1_q), .in1(BanchAdress), .out(multiplexer_1_out), .sel(BranchBoolean));
  Multiplexer #(.select(2), .width(8), .enable("false")) multiplexer_2 (
    .in0(register_1_q), .in1(register_1_q), .in2(register_1_q), .in3(multiplexer_1_out),
    .out(Program_Counter), .sel(CategorieCode));

  // Other names for the same wires on the sheet: BranchAdress[7:0] = BanchAdress; CatCode[1:0] = CategorieCode
endmodule

module ConditionDecoder (
  input  b3,
  input  b2,
  input  b1,
  input  b0,
  input  Zero,
  input  OverFlow,
  input  Negative,
  input  CarryOut,
  output BanchingBoolean
);

  wire and_1_out, and_2_out, and_3_out, and_4_out, and_5_out, and_6_out, and_7_out, and_8_out, and_9_out,
       and_10_out, and_11_out, and_12_out, and_13_out, and_14_out, and_15_out, and_16_out, and_17_out,
       and_18_out, and_19_out, not_1_out, not_2_out, not_3_out, not_4_out, not_5_out, not_6_out, not_7_out,
       not_8_out, not_9_out, not_10_out, not_11_out, not_12_out, not_13_out, not_14_out, not_15_out,
       not_16_out, not_17_out, not_18_out, not_19_out, not_20_out, not_21_out, not_22_out, not_23_out,
       not_24_out, not_25_out, not_26_out, not_27_out, not_28_out, not_29_out, not_30_out, not_31_out,
       not_32_out, not_33_out, not_34_out, not_35_out, not_36_out, not_37_out, not_38_out, not_39_out,
       not_40_out, not_41_out, not_42_out, not_43_out, not_44_out, not_45_out, not_46_out, not_47_out,
       not_48_out, not_49_out;

  not not_1 (not_1_out, b3);
  not not_2 (not_2_out, b2);
  not not_3 (not_3_out, b1);
  not not_4 (not_4_out, b0);
  not not_5 (not_5_out, b3);
  not not_6 (not_6_out, b2);
  not not_7 (not_7_out, b1);
  not not_8 (not_8_out, Zero);
  not not_9 (not_9_out, b3);
  not not_10 (not_10_out, b2);
  not not_11 (not_11_out, b0);
  not not_12 (not_12_out, b3);
  not not_13 (not_13_out, b2);
  not not_14 (not_14_out, CarryOut);
  not not_15 (not_15_out, b3);
  not not_16 (not_16_out, b1);
  not not_17 (not_17_out, b0);
  not not_18 (not_18_out, b0);
  not not_19 (not_19_out, Zero);
  not not_20 (not_20_out, b3);
  not not_21 (not_21_out, b1);
  not not_22 (not_22_out, Negative);
  not not_23 (not_23_out, b1);
  not not_24 (not_24_out, Negative);
  not not_25 (not_25_out, b0);
  not not_26 (not_26_out, b3);
  not not_27 (not_27_out, OverFlow);
  not not_28 (not_28_out, b2);
  not not_29 (not_29_out, b1);
  not not_30 (not_30_out, b0);
  not not_31 (not_31_out, Zero);
  not not_32 (not_32_out, b2);
  not not_33 (not_33_out, b1);
  not not_34 (not_34_out, CarryOut);
  not not_35 (not_35_out, b0);
  not not_36 (not_36_out, OverFlow);
  not not_37 (not_37_out, Negative);
  not not_38 (not_38_out, b0);
  not not_39 (not_39_out, b2);
  not not_40 (not_40_out, OverFlow);
  not not_41 (not_41_out, b2);
  not not_42 (not_42_out, Negative);
  not not_43 (not_43_out, b0);
  not not_44 (not_44_out, Zero);
  not not_45 (not_45_out, OverFlow);
  not not_46 (not_46_out, Negative);
  not not_47 (not_47_out, b1);
  not not_48 (not_48_out, OverFlow);
  not not_49 (not_49_out, b0);
  and and_1 (and_1_out, not_1_out, not_2_out, not_3_out, not_4_out, Zero);
  and and_2 (and_2_out, not_5_out, not_6_out, not_7_out, b0, not_8_out);
  and and_3 (and_3_out, not_9_out, not_10_out, b1, not_11_out, CarryOut);
  and and_4 (and_4_out, not_12_out, not_13_out, b1, b0, not_14_out);
  and and_5 (and_5_out, not_15_out, b2, not_16_out, not_17_out, Negative);
  and and_6 (and_6_out, b2, not_18_out, not_19_out, OverFlow, Negative);
  and and_7 (and_7_out, not_20_out, b2, not_21_out, b0, not_22_out);
  and and_8 (and_8_out, b2, not_23_out, b0, Zero, OverFlow, not_24_out);
  and and_9 (and_9_out, b2, b1, not_25_out, OverFlow);
  and and_10 (and_10_out, not_26_out, b2, b1, b0, not_27_out);
  and and_11 (and_11_out, b3, not_28_out, not_29_out, not_30_out, not_31_out, CarryOut);
  and and_12 (and_12_out, b3, not_32_out, not_33_out, b0, Zero, not_34_out);
  and and_13 (and_13_out, b3, b1, not_35_out, not_36_out, not_37_out);
  and and_14 (and_14_out, b3, b1, not_38_out, OverFlow, Negative);
  and and_15 (and_15_out, b3, not_39_out, b1, b0, not_40_out, Negative);
  and and_16 (and_16_out, b3, not_41_out, b1, b0, OverFlow, not_42_out);
  and and_17 (and_17_out, b3, b2, not_43_out, not_44_out, not_45_out, not_46_out);
  and and_18 (and_18_out, b3, b2, not_47_out, b0, Zero, not_48_out, Negative);
  and and_19 (and_19_out, b3, b2, b1, not_49_out);
  or or_1 (BanchingBoolean, and_1_out, and_2_out, and_3_out, and_4_out, and_5_out, and_6_out, and_7_out, and_8_out, and_9_out, and_10_out, and_11_out, and_12_out, and_13_out, and_14_out, and_15_out, and_16_out, and_17_out, and_18_out, and_19_out);
endmodule

// Sous CategorieB Decoder
module SousCategorieBDecoder (
  input  b9,
  input  b8,
  input  b7,
  input  b6,
  output c3,
  output c2,
  output c1,
  output c0
);

  wire and_1_out, and_2_out, and_3_out, and_5_out, and_6_out, not_1_out, not_2_out, not_3_out, not_4_out,
       not_5_out, not_6_out, not_7_out, not_8_out;

  not not_1 (not_1_out, b7);
  not not_2 (not_2_out, b8);
  not not_3 (not_3_out, b7);
  not not_4 (not_4_out, b8);
  and and_1 (and_1_out, b9, not_4_out, not_5_out);
  not not_5 (not_5_out, b6);
  not not_6 (not_6_out, b8);
  and and_2 (and_2_out, b9, not_6_out, b7);
  not not_7 (not_7_out, b9);
  and and_3 (and_3_out, b8, not_8_out);
  not not_8 (not_8_out, b6);
  and and_4 (c3, b9, b8, not_1_out, b6);
  and and_5 (and_5_out, b9, not_2_out, not_3_out, b6);
  or or_1 (c2, and_5_out, and_6_out);
  and and_6 (and_6_out, b9, b8, b7, b6);
  or or_2 (c1, and_1_out, and_2_out);
  or or_3 (c0, not_7_out, and_3_out);
endmodule
