// Logisim project Ordinateur.circ as structural Verilog: 5 circuits, main circuit Ordinateur
module RAM (
  input  [7:0] DataAdress,
  input  [31:0] DataToStore,
  input  [1:0] LoadStore,
  input  Clock,
  input  Clear,
  output [31:0] DataToLoad
);

  wire Load, loadstoredecoder_1_enableram, not_1_out, Store;

  LoadStoreDecoder loadstoredecoder_1 (
    .ldr(Load), .str(Store), .LdrSignal(LoadStore), .enableram(loadstoredecoder_1_enableram));
  not not_1 (not_1_out, Clock);
  RAM_part #(.dataWidth(32), .bus("separate")) ram_1 (
    .addr(DataAdress), .din(DataToStore), .data(DataToLoad), .str(Store), .sel(loadstoredecoder_1_enableram),
    .clk(not_1_out), .ld(Load), .clr(Clear));

  // Other names for the same wires on the sheet: Reset = Clear
endmodule

module ROM (
  input  [7:0] Instr_Adress,
  output [15:0] Instr
);

  ROM_part #(.dataWidth(16)) rom_1 (.addr(Instr_Adress), .data(Instr));  // open: sel
endmodule

module Ordinateur (
);

  wire ClearRam, clock_1_out, clockcontoler_1_program_terminason, MainClock;
  wire [1:0] LoadStore;
  wire [7:0] DataAdrr, ProgramCounter;
  wire [15:0] InstrFromRom;
  wire [31:0] DataFromRam, DataToRam;

  ROM rom_1 (.Instr_Adress(ProgramCounter), .Instr(InstrFromRom));
  Clock clock_1 (.out(clock_1_out));
  Button Main_Reset (.out(ClearRam));
  // Probe on ProgramCounter
  ClockContoler clockcontoler_1 (
    .ClockIn(clock_1_out), .Instr(InstrFromRom), .ClockOut(MainClock),
    .Program_Terminason(clockcontoler_1_program_terminason), .Clear(ClearRam));
  // Probe on InstrFromRom
  LED Program_Ending (.in(clockcontoler_1_program_terminason));
  Processeur processeur_1 (
    .Reset(ClearRam), .Clock(MainClock), .Instr(InstrFromRom), .Program_Counter(ProgramCounter),
    .DataAdress(DataAdrr), .DataOUt(DataToRam), .DataFRam(DataFromRam), .LoadStore(LoadStore));
  // Probe on LoadStore
  // Probe on DataAdrr
  // Probe on DataToRam
  RAM ram_1 (
    .DataAdress(DataAdrr), .DataToStore(DataToRam), .LoadStore(LoadStore), .Clock(MainClock),
    .Clear(ClearRam), .DataToLoad(DataFromRam));
  // Probe on DataFromRam

  // Other names for the same wires on the sheet: MainReset = ClearRam

  // Notes on the sheet:
  //   ARM-CORTEX M0
endmodule

// Clock Controller
module ClockContoler (
  input  ClockIn,
  input  [15:0] Instr,
  input  Clear,
  output ClockOut,
  output Program_Terminason
);

  wire not_1_out, register_1_q;

  Comparator #(.width(16)) comparator_1 (.a(Instr), .b({16{1'b0}}), .eq(Program_Terminason));  // open: gt, lt
  not not_1 (not_1_out, Program_Terminason);
  Register #(.width(1), .trigger("falling")) register_1 (
    .D(not_1_out), .Q(register_1_q), .clk(ClockIn), .clr(Clear));  // open: en
  and and_1 (ClockOut, ClockIn, register_1_q);
endmodule

// LdrStrDec
module LoadStoreDecoder (
  input  [1:0] LdrSignal,
  output ldr,
  output str,
  output enableram
);

  wire not_1_out;

  and and_1 (ldr, LdrSignal[1], LdrSignal[0]);
  not not_1 (not_1_out, LdrSignal[1]);
  and and_2 (str, not_1_out, LdrSignal[0]);
  or or_1 (enableram, ldr, str);
endmodule
