// Logisim project Processeur.circ as structural Verilog: 1 circuit, main circuit Processeur
module Processeur (
  input  [31:0] DataFRam,
  input  Reset,
  input  Clock,
  input  [15:0] Instr,
  output [7:0] Program_Counter,
  output [7:0] DataAdress,
  output [31:0] DataOUt,
  output [1:0] LoadStore
);

  wire Carry_Value, dataInSelector, LoadImm8, shiftFromRegister;
  wire [2:0] rm, rn;
  wire [3:0] codeOp, flags, rd;
  wire [4:0] imm5;
  wire [7:0] imm8;

  Controller controller_1 (
    .clock(Clock), .reset(Reset), .inst(Instr), .Program_Counter(Program_Counter),
    .DataSelector(dataInSelector), .Load_Store(LoadStore), .Codeop(codeOp), .Rm(rm), .Rn(rn), .Rd(rd),
    .Imm5(imm5), .Imm8(imm8), .LoadImm8(LoadImm8), .Flags(flags), .shiftFromRegistrer(shiftFromRegister),
    .CarryValue(Carry_Value));
  // Probe on codeOp
  CalculUnit calculunit_1 (
    .DataIn_From_Ram(DataFRam), .DataIn_From_Imm8(imm8), .LoadImm8(LoadImm8),
    .DATAinSelecter(dataInSelector), .REGDEST(rd), .clock(Clock), .REGa(rm), .REGb(rn), .Cin(Carry_Value),
    .CODOP(codeOp), .SHIFTER(imm5), .DataOut_TO_Ram(DataOUt), .RESET(Reset), .Flags(flags),
    .ShiftFromRegister(shiftFromRegister));
  // Probe on flags
  Multiplexer #(.select(2), .width(8), .enable("false")) multiplexer_1 (
    .in1(imm8), .in3(imm8), .out(DataAdress), .sel(LoadStore));  // open: in0, in2

  // Other names for the same wires on the sheet: dataFromRam[31:0] = DataFRam; PC[7:0] = Program_Counter
endmodule
