// Logisim project RAM.circ as structural Verilog: 1 circuit, main circuit main
module main (
  input  [7:0] Adress,
  input  [31:0] DataIn,
  input  Enable_Ram,
  input  Load_Store,
  input  Clock_For_store,
  input  Reset_Memory,
  output [31:0] DataOUT
);

  wire not_1_out;

  not not_1 (not_1_out, Load_Store);
  RAM #(.dataWidth(32), .bus("separate")) ram_1 (
    .addr(Adress), .din(DataIn), .data(DataOUT), .str(not_1_out), .sel(Enable_Ram), .clk(Clock_For_store),
    .ld(Load_Store), .clr(Reset_Memory));
endmodule
