// Logisim project ROM.circ as structural Verilog: 1 circuit, main circuit main
// Rom Memory
module main (
  input  [7:0] Instruction_Adress,
  output [15:0] Instruction
);

  ROM #(.dataWidth(16)) rom_1 (.addr(Instruction_Adress), .data(Instruction), .sel(1'b1));

  // Notes on the sheet:
  //   contents of rom_1 (hex, n*v repeats v):
  //   1515 1547
endmodule
