// Logisim project controller.circ as structural Verilog: 9 circuits, main circuit Controller
module Controller (
  input  [15:0] Inst,
  input  [3:0] Flags,
  input  Clk,
  input  Reset,
  output Carry,
  output DP_Shift,
  output Imm32_Enable,
  output [4:0] Imm5,
  output [31:0] Imm32,
  output [3:0] ALU_Opcode,
  output [2:0] Rm,
  output [2:0] Rn,
  output [2:0] Rd,
  output [31:0] RAM_Addr,
  output Load,
  output Store,
  output [7:0] PC
);

  wire Conditional_1_verified, Load_Store_1_pc_hold, not_1_out, Opcode_Decoder_1_conditional,
       Opcode_Decoder_1_data_processing, Opcode_Decoder_1_load_store, Opcode_Decoder_1_shift,
       Opcode_Decoder_1_sp_address, Shift_Add_Sub_Mov_1_carry, SP_Address_1_write_enable;
  wire [2:0] Data_Processing_1_rd, Data_Processing_1_rm, Data_Processing_1_rn, Load_Store_1_rd,
       Load_Store_1_rm, Shift_Add_Sub_Mov_1_rd, Shift_Add_Sub_Mov_1_rm, Shift_Add_Sub_Mov_1_rn;
  wire [3:0] Data_Processing_1_alu_opcode, Data_Processing_1_flags_update_mask, flags_apsr_1_flags_out,
       or_1_out, Shift_Add_Sub_Mov_1_alu_opcode, Shift_Add_Sub_Mov_1_flags_update_mask;
  wire [7:0] adder_1_out, adder_2_out, Conditional_1_offset;
  wire [31:0] SP_Address_1_new_stack_pointer, Stack_Pointer_q;

  Register #(.width(32)) Stack_Pointer (
    .D(SP_Address_1_new_stack_pointer), .en(SP_Address_1_write_enable), .clk(Clk), .Q(Stack_Pointer_q),
    .clr(Reset));
  Opcode_Decoder Opcode_Decoder_1 (
    .Opcode(Inst[15:10]), .Shift(Opcode_Decoder_1_shift), .Data_Processing(Opcode_Decoder_1_data_processing),
    .Load_Store(Opcode_Decoder_1_load_store), .SP_Address(Opcode_Decoder_1_sp_address),
    .Conditional(Opcode_Decoder_1_conditional));
  assign or_1_out = Data_Processing_1_flags_update_mask | Shift_Add_Sub_Mov_1_flags_update_mask;  // OR_Gate or_1, 4 bits wide
  Shift_Add_Sub_Mov Shift_Add_Sub_Mov_1 (
    .Imm32_Enable(Imm32_Enable), .Instruction(Inst), .ALU_Opcode(Shift_Add_Sub_Mov_1_alu_opcode),
    .Enable(Opcode_Decoder_1_shift), .Carry(Shift_Add_Sub_Mov_1_carry),
    .Flags_Update_Mask(Shift_Add_Sub_Mov_1_flags_update_mask), .Rd(Shift_Add_Sub_Mov_1_rd),
    .Rm(Shift_Add_Sub_Mov_1_rm), .Imm5(Imm5), .Imm32(Imm32), .Rn(Shift_Add_Sub_Mov_1_rn));
  Data_Processing Data_Processing_1 (
    .Instruction(Inst), .ALU_Opcode(Data_Processing_1_alu_opcode), .Enable(Opcode_Decoder_1_data_processing),
    .Rm(Data_Processing_1_rm), .Rn(Data_Processing_1_rn), .Rd(Data_Processing_1_rd),
    .Flags_Update_Mask(Data_Processing_1_flags_update_mask));
  Flags_APSR flags_apsr_1 (
    .Flags_In(or_1_out), .Update_Mask(Flags), .Clk(Clk), .Rst(Reset), .Flags_Out(flags_apsr_1_flags_out));
  Load_Store Load_Store_1 (
    .Rm(Load_Store_1_rm), .Rd(Load_Store_1_rd), .Instruction(Inst), .Store(Store),
    .PC_Hold(Load_Store_1_pc_hold), .Reset(Reset), .Enable(Opcode_Decoder_1_load_store), .Load(Load),
    .Clk(Clk), .Stack_Pointer(Stack_Pointer_q), .RAM_Addr(RAM_Addr));
  Conditional Conditional_1 (
    .Instruction(Inst), .Verified(Conditional_1_verified), .Enable(Opcode_Decoder_1_conditional),
    .Offset(Conditional_1_offset), .Z(flags_apsr_1_flags_out[1]), .V(flags_apsr_1_flags_out[3]),
    .N(flags_apsr_1_flags_out[0]), .C(flags_apsr_1_flags_out[2]));
  SP_Address SP_Address_1 (
    .New_Stack_Pointer(SP_Address_1_new_stack_pointer), .Stack_Pointer(Stack_Pointer_q),
    .Enable(Opcode_Decoder_1_sp_address), .Instruction(Inst), .Write_Enable(SP_Address_1_write_enable));
  Adder adder_1 (.a(8'h3), .b(Conditional_1_offset), .out(adder_1_out), .cin(1'b0));  // open: cout
  Adder adder_2 (.a(adder_1_out), .b(PC), .out(adder_2_out), .cin(1'b0));  // open: cout
  and and_1 (DP_Shift, Opcode_Decoder_1_shift, ~Opcode_Decoder_1_data_processing);  // AND_Gate
  not not_1 (not_1_out, Load_Store_1_pc_hold);
  Counter counter_1 (
    .clr(Reset), .load(Conditional_1_verified), .up(1'b1), .count(not_1_out), .clk(Clk), .D(adder_2_out),
    .Q(PC));  // open: carry
  Multiplexer #(.enable("false")) multiplexer_1 (
    .in0(flags_apsr_1_flags_out[1]), .in1(Shift_Add_Sub_Mov_1_carry), .out(Carry), .sel(DP_Shift));
  assign ALU_Opcode = Shift_Add_Sub_Mov_1_alu_opcode | Data_Processing_1_alu_opcode;  // OR_Gate or_2, 4 bits wide
  assign Rm = Shift_Add_Sub_Mov_1_rm | Data_Processing_1_rm | Load_Store_1_rm;  // OR_Gate or_3, 3 bits wide
  assign Rn = Shift_Add_Sub_Mov_1_rn | Data_Processing_1_rn;  // OR_Gate or_4, 3 bits wide
  assign Rd = Shift_Add_Sub_Mov_1_rd | Data_Processing_1_rd | Load_Store_1_rd;  // OR_Gate or_5, 3 bits wide

  // Notes on the sheet:
  //   Extract carry
  //   Extract Opcode
  //   IF Reg_Imm=1 THEN use shift value from register ELSE use shift value from Imm5
  //   Buffer flags for next instruction
  //   Add 3 to offset because ARM pre-increments PC
  //   and does an additionnal prefect operation
  //   Red because Flag in Shift_Update not finished
endmodule

module Conditional (
  input  [15:0] Instruction,
  input  N,
  input  Z,
  input  C,
  input  V,
  input  Enable,
  output [7:0] Offset,
  output Verified
);

  wire conditional_execution_1_enabled;

  Conditional_Execution conditional_execution_1 (
    .Conditions(Instruction[11:8]), .N(N), .Z(Z), .C(C), .V(V), .Enabled(conditional_execution_1_enabled));
  and and_1 (Verified, conditional_execution_1_enabled, Enable);

  assign Offset = Instruction[7:0];
endmodule

module Opcode_Decoder (
  input  [5:0] Opcode,
  output Shift,
  output Data_Processing,
  output Load_Store,
  output SP_Address,
  output Conditional
);

  wire not_1_out, not_2_out, not_3_out, not_4_out, not_5_out, not_6_out, not_7_out, not_8_out, not_9_out,
       not_10_out, not_11_out;

  not not_1 (not_1_out, Opcode[5]);
  not not_2 (not_2_out, Opcode[4]);
  not not_3 (not_3_out, Opcode[5]);
  not not_4 (not_4_out, Opcode[3]);
  not not_5 (not_5_out, Opcode[2]);
  not not_6 (not_6_out, Opcode[1]);
  not not_7 (not_7_out, Opcode[0]);
  not not_8 (not_8_out, Opcode[4]);
  not not_9 (not_9_out, Opcode[3]);
  not not_10 (not_10_out, Opcode[4]);
  not not_11 (not_11_out, Opcode[3]);
  and and_1 (Shift, not_1_out, not_2_out);
  and and_2 (Data_Processing, not_3_out, Opcode[4], not_4_out, not_5_out, not_6_out, not_7_out);
  and and_3 (Load_Store, Opcode[5], not_8_out, not_9_out, Opcode[2]);
  and and_4 (SP_Address, Opcode[5], not_10_out, Opcode[3], Opcode[2]);
  and and_5 (Conditional, Opcode[5], Opcode[4], not_11_out, Opcode[2]);

  // Notes on the sheet:
  //   Shift, add, sub, mov
  //   Load/Store
  //   SP Address
  //   Data Processing
  //   Conditional branch
endmodule

module Data_Processing (
  input  [15:0] Instruction,
  input  Enable,
  output [2:0] Rd,
  output [2:0] Rn,
  output [3:0] Flags_Update_Mask,
  output [2:0] Rm,
  output [3:0] ALU_Opcode
);

  wire [2:0] adder_1_out, and_1_out, subtractor_1_out;
  wire [3:0] multiplexer_3_out;
  wire [3:1] adder_1_cout, subtractor_1_bout;
  wire [3:2] comparator_1_eq;
  wire [15:10] multiplexer_1_out;

  Multiplexer #(.width(16), .enable("false")) multiplexer_1 (
    .in0({16{1'b0}}), .in1(Instruction), .out({multiplexer_1_out, ALU_Opcode, Rn, Rd}), .sel(Enable));
  Multiplexer #(.select(4), .width(3), .enable("false")) multiplexer_2 (
    .in0(3'b000), .in1(3'b000), .in2(3'b000), .in3(3'b000), .in4(3'b000), .in5(3'b000), .in6(3'b000),
    .in7(3'b000), .in8(3'b000), .in9(Rn), .in10(3'b000), .in11(3'b000), .in12(3'b000), .in13(Rn),
    .in14(3'b000), .in15(3'b000), .out(Rm), .sel(ALU_Opcode));
  assign and_1_out = Rn & Rd;  // AND_Gate and_1, 3 bits wide
  Subtractor #(.width(3)) subtractor_1 (
    .a(Rn), .b(Rd), .out(subtractor_1_out), .bout(subtractor_1_bout[1]));  // open: bin
  Adder #(.width(3)) adder_1 (.a(Rn), .b(Rd), .out(adder_1_out), .cout(adder_1_cout[1]));  // open: cin
  Comparator #(.width(3), .mode("unsigned")) comparator_1 (
    .a(3'b000), .b(and_1_out), .gt(comparator_1_eq[3]), .eq(comparator_1_eq[2]));  // open: lt
  Comparator #(.width(3), .mode("unsigned")) comparator_2 (
    .a(3'b000), .b(subtractor_1_out), .gt(subtractor_1_bout[3]), .eq(subtractor_1_bout[2]));  // open: lt
  Comparator #(.width(3), .mode("unsigned")) comparator_3 (
    .a(3'b000), .b(adder_1_out), .gt(adder_1_cout[3]), .eq(adder_1_cout[2]));  // open: lt
  Multiplexer #(.select(4), .width(4), .enable("false")) multiplexer_3 (
    .in0({comparator_1_eq, 2'b00}), .in1(4'b0000), .in2(4'b0000), .in3(4'b0000), .in4(4'b0000),
    .in5(4'b0000), .in6(4'b0000), .in7(4'b0000), .in8(4'b0000), .in9({subtractor_1_bout, 1'b0}),
    .in10({adder_1_cout, 1'b0}), .in11(4'b0000), .in12(4'b0000), .in13(4'b0000), .in14(4'b0000),
    .in15(4'b0000), .out(multiplexer_3_out), .sel(ALU_Opcode));
  Multiplexer #(.width(4), .enable("false")) multiplexer_4 (
    .in0(4'b0000), .in1(multiplexer_3_out), .out(Flags_Update_Mask), .sel(Enable));

  // Notes on the sheet:
  //   Note 2: RSB instruction has Rn as 1st operand.
  //   MUL instruction has Rn as 1st operand and Rdm as 2nd operand
  //   Pull output low on Enable = 0
  //   For simplification purposes, Rm is used for 1st operand both here and in the ALU.
  //   Note: instructions that does not save the result will still have the second operand as the destination register, the ALU will copy the second register to the destination register
endmodule

module Shift_Add_Sub_Mov (
  input  [15:0] Instruction,
  input  Enable,
  output [3:0] Flags_Update_Mask,
  output Carry,
  output [2:0] Rm,
  output [2:0] Rd,
  output [2:0] Rn,
  output [4:0] Imm5,
  output [31:0] Imm32,
  output Imm32_Enable,
  output [3:0] ALU_Opcode
);

  wire and_1_out, and_2_out;
  wire [2:0] multiplexer_7_out;
  wire [3:0] multiplexer_3_out;
  wire [7:0] multiplexer_9_out;
  wire [15:0] multiplexer_1_out;
  wire [31:0] bit_extender_1_out, bit_extender_2_out;

  Multiplexer #(.width(16), .enable("false")) multiplexer_1 (
    .in0({16{1'b0}}), .in1(Instruction), .out(multiplexer_1_out), .sel(Enable));
  Multiplexer #(.width(3), .enable("false")) multiplexer_2 (
    .in0(multiplexer_1_out[5:3]), .in1(3'b000), .out(Rn), .sel(multiplexer_1_out[13]));
  Multiplexer #(.width(4), .enable("false")) multiplexer_3 (
    .in0(4'b0101), .in1(4'b0110), .out(multiplexer_3_out), .sel(multiplexer_1_out[9]));
  Multiplexer #(.select(3), .width(5), .enable("false")) multiplexer_4 (
    .in0(multiplexer_1_out[10:6]), .in1(multiplexer_1_out[10:6]), .in2(multiplexer_1_out[10:6]),
    .in3({5{1'b0}}), .in4({5{1'b0}}), .in5({5{1'b0}}), .in6({5{1'b0}}), .in7({5{1'b0}}), .out(Imm5),
    .sel(multiplexer_1_out[13:11]));
  Multiplexer #(.select(3), .width(3), .enable("false")) multiplexer_5 (
    .in0(multiplexer_1_out[5:3]), .in1(multiplexer_1_out[5:3]), .in2(multiplexer_1_out[5:3]),
    .in3(multiplexer_1_out[8:6]), .in4(3'b000), .in5(3'b000), .in6(3'b000), .in7(3'b000), .out(Rm),
    .sel(multiplexer_1_out[13:11]));
  Multiplexer #(.width(3), .enable("false")) multiplexer_6 (
    .in0(multiplexer_1_out[2:0]), .in1(multiplexer_1_out[10:8]), .out(Rd), .sel(multiplexer_1_out[13]));
  and and_1 (and_1_out, multiplexer_1_out[11], multiplexer_1_out[12]);
  and and_2 (and_2_out, multiplexer_1_out[10], and_1_out);
  Multiplexer #(.width(3), .enable("false")) multiplexer_7 (
    .in0(3'b000), .in1(multiplexer_1_out[8:6]), .out(multiplexer_7_out), .sel(and_2_out));
  or or_1 (Imm32_Enable, and_2_out, multiplexer_1_out[13]);
  Multiplexer #(.select(2), .width(4), .enable("false")) multiplexer_8 (
    .in0(4'b0010), .in1(4'b0011), .in2(4'b0100), .in3(multiplexer_3_out), .out(ALU_Opcode),
    .sel(multiplexer_1_out[12:11]));
  assign bit_extender_1_out = {{29{1'b0}}, multiplexer_7_out};  // Bit_Extender bit_extender_1
  Multiplexer #(.width(8), .enable("false")) multiplexer_9 (
    .in0({8{1'b0}}), .in1(multiplexer_1_out[7:0]), .out(multiplexer_9_out), .sel(multiplexer_1_out[13]));
  assign bit_extender_2_out = {{24{1'b0}}, multiplexer_9_out};  // Bit_Extender bit_extender_2
  assign Imm32 = bit_extender_1_out | bit_extender_2_out;  // OR_Gate or_2, 32 bits wide

  // Notes on the sheet:
  //   Pull output low on Enable = 0
  //   Note 3: Imm32_Enable forces the use of the immediate for Rm register (MOV ADD SUB imm)
  //   Note: ALU uses Rn register for shifts. Use Rn instead of Rm for shifts (immediate) here too
  //   Note 2: MOV uses RSB ALU opcode with Imm8 reversed so that it is copied to output register
  //   pin9
  //   Enable carry for SUB since it is reversed in ALU
  //   ALU will use Imm32 instead of Rm
endmodule

module Load_Store (
  input  [15:0] Instruction,
  input  Reset,
  input  Enable,
  input  Clk,
  input  [31:0] Stack_Pointer,
  output [2:0] Rm,
  output [2:0] Rd,
  output Store,
  output PC_Hold,
  output Load,
  output [31:0] RAM_Addr
);

  wire and_1_out, not_1_out, not_2_out, not_3_out;
  wire [7:0] imm8;
  wire [15:8] multiplexer_1_out;
  wire [31:0] adder_1_out, multiplexer_2_out;

  not not_1 (not_1_out, Reset);
  Multiplexer #(.width(16), .enable("false")) multiplexer_1 (
    .in0({16{1'b0}}), .in1(Instruction), .out({multiplexer_1_out, imm8}), .sel(and_1_out));
  and and_1 (and_1_out, not_1_out, Enable);
  Multiplexer #(.width(32), .enable("false")) multiplexer_2 (
    .in0({32{1'b0}}), .in1(Stack_Pointer), .out(multiplexer_2_out), .sel(and_1_out));
  Demultiplexer #(.width(3), .enable("false")) demultiplexer_1 (
    .out0(Rm), .out1(Rd), .in(multiplexer_1_out[10:8]), .sel(multiplexer_1_out[11]));
  not not_2 (not_2_out, Clk);
  Adder #(.width(32)) adder_1 (.a({{24{1'b0}}, imm8}), .b(multiplexer_2_out), .out(adder_1_out));  // open: cin, cout
  and and_2 (Store, multiplexer_1_out[11], Clk);
  D_Flip_Flop d_ff_1 (.D(not_3_out), .clk(Clk), .Q(PC_Hold), .Qn(Load));  // open: preset, reset
  not not_3 (not_3_out, multiplexer_1_out[11]);
  Multiplexer #(.width(32), .enable("false")) multiplexer_3 (
    .in0(adder_1_out), .in1(Stack_Pointer), .out(RAM_Addr), .sel(not_2_out));

  // Notes on the sheet:
  //   Delay load and hold PC for 1 cycle for the RAM to send out requested data 
endmodule

module SP_Address (
  input  [31:0] Stack_Pointer,
  input  [15:0] Instruction,
  input  Enable,
  output [31:0] New_Stack_Pointer,
  output Write_Enable
);

  wire comparator_1_eq, not_1_out;
  wire [31:0] adder_1_out, multiplexer_1_out, subtractor_1_out;

  Adder #(.width(32)) adder_1 (
    .a(Stack_Pointer), .b({{25{1'b0}}, Instruction[6:0]}), .out(adder_1_out));  // open: cin, cout
  Subtractor #(.width(32)) subtractor_1 (
    .a(Stack_Pointer), .b({{25{1'b0}}, Instruction[6:0]}), .out(subtractor_1_out));  // open: bin, bout
  Multiplexer #(.width(32), .enable("false")) multiplexer_1 (
    .in0(adder_1_out), .in1(subtractor_1_out), .out(multiplexer_1_out), .sel(Instruction[7]));
  Comparator #(.width(32)) comparator_1 (
    .a(multiplexer_1_out), .b(Stack_Pointer), .eq(comparator_1_eq));  // open: gt, lt
  not not_1 (not_1_out, comparator_1_eq);
  Multiplexer #(.width(32), .enable("false")) multiplexer_2 (
    .in0({32{1'b0}}), .in1(multiplexer_1_out), .out(New_Stack_Pointer), .sel(Enable));
  Multiplexer #(.enable("false")) multiplexer_3 (.in0(1'b0), .in1(not_1_out), .out(Write_Enable), .sel(Enable));

  // Notes on the sheet:
  //   Pull output low on Enable = 0
endmodule

module Flags_APSR (
  input  [3:0] Flags_In,
  input  [3:0] Update_Mask,
  input  Clk,
  input  Rst,
  output [3:0] Flags_Out
);

  wire not_1_out, not_2_out, not_3_out, not_4_out, up1, up2, up3, up4;
  wire [3:0] multiplexer_1_out;

  Register #(.width(4)) register_1 (.D(Update_Mask), .en(1'b1), .clk(Clk), .Q({up4, up3, up2, up1}), .clr(1'b0));
  Multiplexer #(.enable("false")) multiplexer_1 (
    .in0(Flags_In[0]), .in1(not_1_out), .out(multiplexer_1_out[0]), .sel(up1));
  not not_1 (not_1_out, Flags_In[0]);
  Multiplexer #(.enable("false")) multiplexer_2 (
    .in0(Flags_In[1]), .in1(not_2_out), .out(multiplexer_1_out[1]), .sel(up2));
  not not_2 (not_2_out, Flags_In[1]);
  Multiplexer #(.enable("false")) multiplexer_3 (
    .in0(Flags_In[2]), .in1(not_3_out), .out(multiplexer_1_out[2]), .sel(up3));
  not not_3 (not_3_out, Flags_In[2]);
  Multiplexer #(.enable("false")) multiplexer_4 (
    .in0(Flags_In[3]), .in1(not_4_out), .out(multiplexer_1_out[3]), .sel(up4));
  not not_4 (not_4_out, Flags_In[3]);
  Multiplexer #(.width(4), .enable("false")) multiplexer_5 (
    .in0(multiplexer_1_out), .in1(4'b0000), .out(Flags_Out), .sel(Rst));
endmodule

module Conditional_Execution (
  input  [3:0] Conditions,
  input  N,
  input  Z,
  input  C,
  input  V,
  output Enabled
);

  wire and_1_out, and_2_out, and_3_out, and_4_out, and_5_out, and_6_out, and_7_out, and_8_out, and_9_out,
       and_10_out, and_11_out, and_12_out, and_13_out, and_14_out, and_15_out, and_16_out, and_17_out,
       even_parity_1_out, not_1_out, not_2_out, not_3_out, not_4_out, not_5_out, not_6_out, not_7_out,
       not_8_out, not_9_out, not_10_out, not_11_out, not_12_out, not_13_out, not_14_out, not_15_out,
       not_16_out, not_17_out, not_18_out, not_19_out, not_20_out, not_21_out, not_22_out, not_23_out,
       not_24_out, not_25_out, not_26_out, not_27_out, not_28_out, not_29_out, not_30_out, not_31_out,
       not_32_out, not_33_out, not_34_out, not_35_out, not_36_out, not_37_out, not_38_out, not_39_out,
       not_40_out, not_41_out, not_42_out, odd_parity_1_out, or_1_out, or_2_out;

  and and_1 (and_1_out, C, not_1_out);
  not not_1 (not_1_out, Z);
  not not_2 (not_2_out, C);
  or or_1 (or_1_out, not_2_out, Z);
  xnor even_parity_1 (even_parity_1_out, N, V);
  xor odd_parity_1 (odd_parity_1_out, N, V);
  and and_2 (and_2_out, even_parity_1_out, not_3_out);
  not not_3 (not_3_out, Z);
  or or_2 (or_2_out, odd_parity_1_out, Z);
  not not_4 (not_4_out, Conditions[3]);
  not not_5 (not_5_out, Conditions[2]);
  not not_6 (not_6_out, Conditions[1]);
  not not_7 (not_7_out, Conditions[0]);
  not not_8 (not_8_out, Conditions[3]);
  not not_9 (not_9_out, Conditions[2]);
  not not_10 (not_10_out, Z);
  not not_11 (not_11_out, Conditions[1]);
  not not_12 (not_12_out, Conditions[3]);
  not not_13 (not_13_out, Conditions[2]);
  not not_14 (not_14_out, Conditions[0]);
  not not_15 (not_15_out, Conditions[3]);
  not not_16 (not_16_out, Conditions[2]);
  not not_17 (not_17_out, C);
  not not_18 (not_18_out, Conditions[3]);
  not not_19 (not_19_out, Conditions[1]);
  not not_20 (not_20_out, Conditions[0]);
  not not_21 (not_21_out, Conditions[3]);
  not not_22 (not_22_out, N);
  not not_23 (not_23_out, Conditions[1]);
  not not_24 (not_24_out, Conditions[3]);
  not not_25 (not_25_out, Conditions[0]);
  not not_26 (not_26_out, Conditions[3]);
  not not_27 (not_27_out, V);
  not not_28 (not_28_out, Conditions[2]);
  not not_29 (not_29_out, Conditions[1]);
  not not_30 (not_30_out, Conditions[0]);
  not not_31 (not_31_out, Conditions[2]);
  not not_32 (not_32_out, Conditions[1]);
  not not_33 (not_33_out, Conditions[2]);
  not not_34 (not_34_out, Conditions[0]);
  not not_35 (not_35_out, Conditions[2]);
  not not_36 (not_36_out, Conditions[1]);
  not not_37 (not_37_out, Conditions[0]);
  not not_38 (not_38_out, Conditions[3]);
  not not_39 (not_39_out, Conditions[2]);
  not not_40 (not_40_out, Conditions[1]);
  not not_41 (not_41_out, Conditions[0]);
  not not_42 (not_42_out, Conditions[0]);
  and and_3 (and_3_out, not_4_out, not_5_out, Z, not_6_out, not_7_out);
  and and_4 (and_4_out, not_8_out, not_9_out, not_10_out, not_11_out, Conditions[0]);
  and and_5 (and_5_out, not_12_out, not_13_out, C, Conditions[1], not_14_out);
  and and_6 (and_6_out, not_15_out, not_16_out, not_17_out, Conditions[1], Conditions[0]);
  and and_7 (and_7_out, not_18_out, Conditions[2], N, not_19_out, not_20_out);
  and and_8 (and_8_out, not_21_out, Conditions[2], not_22_out, not_23_out, Conditions[0]);
  and and_9 (and_9_out, not_24_out, Conditions[2], V, Conditions[1], not_25_out);
  and and_10 (and_10_out, not_26_out, Conditions[2], not_27_out, Conditions[1], Conditions[0]);
  and and_11 (and_11_out, Conditions[3], not_28_out, and_1_out, not_29_out, not_30_out);
  and and_12 (and_12_out, Conditions[3], not_31_out, or_1_out, not_32_out, Conditions[0]);
  and and_13 (and_13_out, Conditions[3], not_33_out, even_parity_1_out, Conditions[1], not_34_out);
  and and_14 (and_14_out, Conditions[3], not_35_out, odd_parity_1_out, Conditions[1], Conditions[0]);
  and and_15 (and_15_out, Conditions[3], Conditions[2], and_2_out, not_36_out, not_37_out);
  and and_16 (and_16_out, not_38_out, not_39_out, or_2_out, not_40_out, not_41_out);
  and and_17 (and_17_out, Conditions[3], Conditions[2], 1'b1, Conditions[1], not_42_out);
  or or_3 (Enabled, and_3_out, and_4_out, and_5_out, and_6_out, and_7_out, and_8_out, and_9_out, and_10_out, and_11_out, and_12_out, and_13_out, and_14_out, and_15_out, and_16_out, and_17_out);

  // Notes on the sheet:
  //   Equal
  //   Not Equal
  //   Carry set
  //   Carry clear
  //   Minus, negative
  //   Overflow
  //   No overflow
  //   Unsigned higher
  //   Signed less than
  //   Signed greater than
  //   Always
  //   Plus, positive or zero
  //   Unsigned lower or same
  //   Signed greater than or equal
  //   Signed less than or equal
endmodule
