// Logisim project ALU.circ as structural Verilog: 2 circuits, main circuit ALU
module ALU (
  input  [4:0] Shift,
  input  [31:0] A,
  input  [31:0] B,
  input  CarryIn,
  input  [3:0] Codop,
  output [3:0] Flags,
  output [31:0] S
);

  wire and_3_out, and_4_out, bitselector_4_out, bitselector_5_out, bitselector_6_out, C3, C4_5, C6, C7, C8,
       C10, C11, C12, comparator_2_gt, not_1_out, not_4_out, not_5_out, xor_1_out, xor_2_out;
  wire [4:0] negator_1_out, subtractor_4_out;
  wire [31:0] AAND, ADC, ASR, BIC, CMN, CMP, EOR, LSL, LSR, MUL, MVN, not_2_out, ORR, RROR, RSB, SBC, TST;

  // Probe on A
  assign AAND = A & B;  // AND_Gate AAND, 32 bits wide
  assign EOR = A ^ B;  // XOR_Gate EOR, 32 bits wide
  Shifter #(.width(32)) shifter_1 (.in(B), .\dist (Shift), .out(LSL));
  Shifter #(.width(32), .shift("lr")) shifter_2 (.in(B), .\dist (Shift), .out(LSR));
  Shifter #(.width(32), .shift("ar")) shifter_3 (.in(B), .\dist (Shift), .out(ASR));
  Adder #(.width(32)) adder_1 (.a(B), .b(A), .out(ADC), .cin(CarryIn), .cout(C6));
  not not_1 (not_1_out, CarryIn);
  Subtractor #(.width(32)) subtractor_1 (.a(B), .b(A), .out(SBC), .bin(not_1_out), .bout(C7));
  Shifter #(.width(32), .shift("rl")) shifter_4 (.in(B), .\dist (Shift), .out(RROR));
  // Probe on B
  assign TST = A & B;  // AND_Gate and_1, 32 bits wide
  Subtractor #(.width(32)) subtractor_2 (.a({32{1'b0}}), .b(A), .out(RSB), .bout(C10));  // open: bin
  Subtractor #(.width(32)) subtractor_3 (.a(A), .b(B), .out(CMP), .bout(C11));  // open: bin
  Adder #(.width(32)) adder_2 (.a(A), .b(B), .out(CMN), .cout(C12));  // open: cin
  assign ORR = A | B;  // OR_Gate or_1, 32 bits wide
  assign not_2_out = ~B;  // NOT_Gate not_2, 32 bits wide
  assign MVN = ~B;  // NOT_Gate not_3, 32 bits wide
  Multi32 multi32_1 (.in_1(A), .in_2(B), .out_3(MUL));
  assign BIC = A & not_2_out;  // AND_Gate and_2, 32 bits wide
  Negator #(.width(5)) negator_1 (.in(Shift), .out(negator_1_out));
  BitSelector #(.width(32)) bitselector_1 (.in(B), .out(C3), .sel(negator_1_out));
  Subtractor #(.width(5)) subtractor_4 (.a(Shift), .b(5'b00001), .out(subtractor_4_out));  // open: bin, bout
  BitSelector #(.width(32)) bitselector_2 (.in(B), .out(C4_5), .sel(subtractor_4_out));
  BitSelector #(.width(32)) bitselector_3 (.in(S), .out(C8), .sel({5{1'b1}}));
  BitSelector #(.width(32)) bitselector_4 (.in(A), .out(bitselector_4_out), .sel({5{1'b1}}));
  BitSelector #(.width(32)) bitselector_5 (.in(B), .out(bitselector_5_out), .sel({5{1'b1}}));
  BitSelector #(.width(32)) bitselector_6 (.in(S), .out(bitselector_6_out), .sel({5{1'b1}}));
  Multiplexer #(.select(4), .width(32), .enable("false")) multiplexer_1 (
    .in0(AAND), .in1(EOR), .in2(LSL), .in3(LSR), .in4(ASR), .in5(ADC), .in6(SBC), .in7(RROR), .in8(TST),
    .in9(RSB), .in10(CMP), .in11(CMN), .in12(ORR), .in13(MUL), .in14(BIC), .in15(MVN), .out(S), .sel(Codop));
  Comparator #(.width(32)) comparator_1 (.a(S), .b({32{1'b0}}), .eq(Flags[2]), .lt(Flags[3]));  // open: gt
  xor xor_1 (xor_1_out, bitselector_4_out, bitselector_5_out);
  xor xor_2 (xor_2_out, bitselector_5_out, bitselector_6_out);
  // Probe on S
  Multiplexer #(.select(4), .enable("false")) multiplexer_2 (
    .in0(1'b0), .in1(1'b0), .in2(C3), .in3(C4_5), .in4(C4_5), .in5(C6), .in6(C7), .in7(C8), .in8(1'b0),
    .in9(C10), .in10(C11), .in11(C12), .in12(1'b0), .in13(1'b0), .in14(1'b0), .in15(1'b0), .out(Flags[1]),
    .sel(Codop));
  not not_4 (not_4_out, xor_1_out);
  not not_5 (not_5_out, xor_2_out);
  Comparator #(.width(32)) comparator_2 (.a(B), .b(S), .gt(comparator_2_gt));  // open: eq, lt
  and and_3 (and_3_out, not_4_out, xor_2_out);
  and and_4 (and_4_out, xor_1_out, not_5_out);
  Multiplexer #(.select(4), .enable("false")) multiplexer_3 (
    .in0(1'b0), .in1(1'b0), .in2(comparator_2_gt), .in3(1'b0), .in4(1'b0), .in5(and_3_out), .in6(and_4_out),
    .in7(comparator_2_gt), .in8(1'b0), .in9(1'b0), .in10(and_4_out), .in11(and_3_out), .in12(1'b0),
    .in13(and_3_out), .in14(1'b0), .in15(1'b0), .out(Flags[0]), .sel(Codop));

  // Other names for the same wires on the sheet: V = Flags[0]; C = Flags[1]; Z = Flags[2]; N = Flags[3];
  //   Ouutput[31:0] = S
endmodule

module Multi32 (
  input  [31:0] in_1,
  input  [31:0] in_2,
  output [31:0] out_3
);

  wire [15:0] adder_1_out, bitselector_1_out, bitselector_2_out, bitselector_3_out, bitselector_4_out,
       multiplier_1_cout, multiplier_1_out, multiplier_2_out, multiplier_3_out;
  wire [31:0] bit_extender_1_out, bit_extender_2_out, shifter_1_out;

  // Probe on in_1
  // Probe on in_2
  // Probe on bitselector_1_out
  BitSelector #(.width(32), .group(16)) bitselector_1 (.in(in_1), .out(bitselector_1_out), .sel(1'b0));
  BitSelector #(.width(32), .group(16)) bitselector_2 (.in(in_1), .out(bitselector_2_out), .sel(1'b1));
  BitSelector #(.width(32), .group(16)) bitselector_3 (.in(in_2), .out(bitselector_3_out), .sel(1'b0));
  BitSelector #(.width(32), .group(16)) bitselector_4 (.in(in_2), .out(bitselector_4_out), .sel(1'b1));
  // Probe on bitselector_3_out
  // Probe on bitselector_2_out
  // Probe on bitselector_4_out
  // Probe on multiplier_1_out
  // Probe on multiplier_1_cout
  Multiplier #(.width(16)) multiplier_1 (
    .a(bitselector_1_out), .b(bitselector_3_out), .out(multiplier_1_out), .cout(multiplier_1_cout));  // open: cin
  Multiplier #(.width(16)) multiplier_2 (
    .a(bitselector_1_out), .b(bitselector_4_out), .out(multiplier_2_out), .cin(multiplier_1_cout));  // open: cout
  Multiplier #(.width(16)) multiplier_3 (
    .a(bitselector_2_out), .b(bitselector_3_out), .out(multiplier_3_out));  // open: cin, cout
  // Probe on multiplier_2_out
  Adder #(.width(16)) adder_1 (.a(multiplier_2_out), .b(multiplier_3_out), .out(adder_1_out));  // open: cin, cout
  // Probe on multiplier_3_out
  // Probe on bit_extender_1_out
  assign bit_extender_1_out = {{16{1'b0}}, multiplier_1_out};  // Bit_Extender bit_extender_1
  assign bit_extender_2_out = {{16{1'b0}}, adder_1_out};  // Bit_Extender bit_extender_2
  // Probe on bit_extender_2_out
  Shifter #(.width(32)) shifter_1 (.in(bit_extender_2_out), .\dist (5'b10000), .out(shifter_1_out));
  // Probe on shifter_1_out
  // Probe on out_3
  assign out_3 = bit_extender_1_out | shifter_1_out;  // OR_Gate or_1, 32 bits wide
endmodule
