// Logisim project BancDeRegistre.circ as structural Verilog: 1 circuit, main circuit BancRegistre
module BancRegistre (
  input  [31:0] DataIn,
  input  [2:0] RegA,
  input  in_3,
  input  [2:0] RegDest,
  input  [2:0] RegB,
  input  in_6,
  output [31:0] R0,
  output [31:0] R1,
  output [31:0] AOut,
  output [31:0] R2,
  output [31:0] R3,
  output [31:0] R4,
  output [31:0] R5,
  output [31:0] R6,
  output [31:0] BOut,
  output [31:0] R7
);

  wire demultiplexer_1_out0, demultiplexer_1_out1, demultiplexer_1_out2, demultiplexer_1_out3,
       demultiplexer_1_out4, demultiplexer_1_out5, demultiplexer_1_out6, demultiplexer_1_out7;

  Demultiplexer #(.select(3)) demultiplexer_1 (
    .out0(demultiplexer_1_out0), .out1(demultiplexer_1_out1), .out2(demultiplexer_1_out2),
    .out3(demultiplexer_1_out3), .out4(demultiplexer_1_out4), .out5(demultiplexer_1_out5),
    .out6(demultiplexer_1_out6), .out7(demultiplexer_1_out7), .in(in_3), .sel(RegDest));  // open: en
  Register #(.width(32)) u_R0 (.D(DataIn), .Q(R0), .clk(demultiplexer_1_out0), .clr(in_6));  // open: en
  Register #(.width(32)) u_R1 (.D(DataIn), .Q(R1), .clk(demultiplexer_1_out1), .clr(in_6));  // open: en
  Register #(.width(32)) u_R7 (.D(DataIn), .Q(R2), .clk(demultiplexer_1_out2), .clr(in_6));  // open: en
  Register #(.width(32)) u_R3 (.D(DataIn), .Q(R3), .clk(demultiplexer_1_out3), .clr(in_6));  // open: en
  Register #(.width(32)) u_R4 (.D(DataIn), .Q(R4), .clk(demultiplexer_1_out4), .clr(in_6));  // open: en
  Register #(.width(32)) u_R5 (.D(DataIn), .Q(R5), .clk(demultiplexer_1_out5), .clr(in_6));  // open: en
  Register #(.width(32)) u_R6 (.D(DataIn), .Q(R6), .clk(demultiplexer_1_out6), .clr(in_6));  // open: en
  Register #(.width(32)) R7_2 (.D(DataIn), .Q(R7), .clk(demultiplexer_1_out7), .clr(in_6));  // open: en
  Multiplexer #(.select(3), .width(32)) multiplexer_1 (
    .in0(R0), .in1(R1), .in2(R2), .in3(R3), .in4(R4), .in5(R5), .in6(R6), .in7(R7), .out(AOut), .sel(RegA));  // open: en
  Multiplexer #(.select(3), .width(32)) multiplexer_2 (
    .in0(R0), .in1(R1), .in2(R2), .in3(R3), .in4(R4), .in5(R5), .in6(R6), .in7(R7), .out(BOut), .sel(RegB));  // open: en

  // Other names for the same wires on the sheet: DataOut0[31:0] = R0; DataOut1[31:0] = R1; DataOut2[31:0] = R2;
  //   DataOut3[31:0] = R3; DataOut4[31:0] = R4; DataOut5[31:0] = R5; DataOut6[31:0] = R6; DataOut7[31:0] = R7
endmodule
