// Logisim project BancDeRegistres.circ as structural Verilog: 1 circuit, main circuit BancRegistre
module BancRegistre (
  input  [31:0] DataIn,
  input  Clk,
  input  Reset,
  input  [2:0] RegA,
  input  [2:0] RegDest,
  input  [2:0] RegB,
  output [31:0] AOut,
  output [31:0] BOut,
  output [31:0] R0,
  output [31:0] R1,
  output [31:0] R2,
  output [31:0] R3,
  output [31:0] R4,
  output [31:0] R5,
  output [31:0] R6,
  output [31:0] R7
);

  wire demultiplexer_1_out0, demultiplexer_1_out1, demultiplexer_1_out2, demultiplexer_1_out3,
       demultiplexer_1_out4, demultiplexer_1_out5, demultiplexer_1_out6, demultiplexer_1_out7;

  Demultiplexer #(.select(3), .enable("false")) demultiplexer_1 (
    .out0(demultiplexer_1_out0), .out1(demultiplexer_1_out1), .out2(demultiplexer_1_out2),
    .out3(demultiplexer_1_out3), .out4(demultiplexer_1_out4), .out5(demultiplexer_1_out5),
    .out6(demultiplexer_1_out6), .out7(demultiplexer_1_out7), .in(1'b1), .sel(RegDest));
  Register #(.width(32)) register_1 (.D(DataIn), .en(demultiplexer_1_out0), .clk(Clk), .Q(R0), .clr(Reset));
  Register #(.width(32)) register_2 (.D(DataIn), .en(demultiplexer_1_out1), .clk(Clk), .Q(R1), .clr(Reset));
  Register #(.width(32)) register_3 (.D(DataIn), .en(demultiplexer_1_out2), .clk(Clk), .Q(R2), .clr(Reset));
  Register #(.width(32)) register_4 (.D(DataIn), .en(demultiplexer_1_out3), .clk(Clk), .Q(R3), .clr(Reset));
  Register #(.width(32)) register_5 (.D(DataIn), .en(demultiplexer_1_out4), .clk(Clk), .Q(R4), .clr(Reset));
  Register #(.width(32)) register_6 (.D(DataIn), .en(demultiplexer_1_out5), .clk(Clk), .Q(R5), .clr(Reset));
  Register #(.width(32)) register_7 (.D(DataIn), .en(demultiplexer_1_out6), .clk(Clk), .Q(R6), .clr(Reset));
  Register #(.width(32)) register_8 (.D(DataIn), .en(demultiplexer_1_out7), .clk(Clk), .Q(R7), .clr(Reset));
  Multiplexer #(.select(3), .width(32)) multiplexer_1 (
    .in0(R0), .in1(R1), .in2(R2), .in3(R3), .in4(R4), .in5(R5), .in6(R6), .in7(R7), .out(AOut), .sel(RegA));  // open: en
  Multiplexer #(.select(3), .width(32)) multiplexer_2 (
    .in0(R0), .in1(R1), .in2(R2), .in3(R3), .in4(R4), .in5(R5), .in6(R6), .in7(R7), .out(BOut), .sel(RegB));  // open: en

  // Other names for the same wires on the sheet: DataOut0[31:0] = R0; DataOut1[31:0] = R1; DataOut2[31:0] = R2;
  //   DataOut3[31:0] = R3; DataOut4[31:0] = R4; DataOut5[31:0] = R5; DataOut6[31:0] = R6; DataOut7[31:0] = R7
endmodule
