// Logisim project Controller.circ as structural Verilog: 18 circuits, main circuit Controller
module Controller (
  input  [15:0] Inst,
  input  [3:0] Flags,
  input  Clk,
  input  Reset,
  output Carry,
  output DP_Shift,
  output Imm32_Enable,
  output [4:0] Imm5,
  output [31:0] Imm32,
  output [3:0] ALU_Opcode,
  output [2:0] Rm,
  output [2:0] Rn,
  output [2:0] Rd,
  output [31:0] RAM_Addr,
  output Load,
  output Store,
  output [7:0] PC
);

  wire Conditional_1_verified, Load_Store_1_pc_hold, not_1_out, Opcode_Decoder_1_conditional,
       Opcode_Decoder_1_data_processing, Opcode_Decoder_1_load_store, Opcode_Decoder_1_shift,
       Opcode_Decoder_1_sp_address, Shift_Add_Sub_Mov_1_carry, SP_Address_1_write_enable;
  wire [2:0] Data_Processing_1_rd, Data_Processing_1_rm, Data_Processing_1_rn, Load_Store_1_rd,
       Load_Store_1_rm, Shift_Add_Sub_Mov_1_rd, Shift_Add_Sub_Mov_1_rm, Shift_Add_Sub_Mov_1_rn;
  wire [3:0] Data_Processing_1_flags_update_mask, Data_Processing_1_opcode, flags_apsr_1_flags_out, or_1_out,
       Shift_Add_Sub_Mov_1_alu_opcode, Shift_Add_Sub_Mov_1_flags_update_mask;
  wire [7:0] Conditional_1_offset, subtractor_1_out;
  wire [31:0] SP_Address_1_new_stack_pointer, Stack_Pointer_q;

  Register #(.width(32)) Stack_Pointer (
    .D(SP_Address_1_new_stack_pointer), .en(SP_Address_1_write_enable), .clk(Clk), .Q(Stack_Pointer_q),
    .clr(Reset));
  Opcode_Decoder Opcode_Decoder_1 (
    .Opcode(Inst[15:10]), .Shift(Opcode_Decoder_1_shift), .Data_Processing(Opcode_Decoder_1_data_processing),
    .Load_Store(Opcode_Decoder_1_load_store), .SP_Address(Opcode_Decoder_1_sp_address),
    .Conditional(Opcode_Decoder_1_conditional));
  assign or_1_out = Data_Processing_1_flags_update_mask | Shift_Add_Sub_Mov_1_flags_update_mask;  // OR_Gate or_1, 4 bits wide
  Shift_Add_Sub_Mov Shift_Add_Sub_Mov_1 (
    .Rn(Shift_Add_Sub_Mov_1_rn), .Instruction(Inst), .Enable(Opcode_Decoder_1_shift), .Imm5(Imm5),
    .Rm(Shift_Add_Sub_Mov_1_rm), .Rd(Shift_Add_Sub_Mov_1_rd), .Imm32_Enable(Imm32_Enable), .out_8(Imm32),
    .ALU_Opcode(Shift_Add_Sub_Mov_1_alu_opcode), .Carry(Shift_Add_Sub_Mov_1_carry),
    .Flags_Update_Mask(Shift_Add_Sub_Mov_1_flags_update_mask));
  Data_Processing Data_Processing_1 (
    .Instructions(Inst), .Rn(Data_Processing_1_rn), .Enable(Opcode_Decoder_1_data_processing),
    .Rm(Data_Processing_1_rm), .Rd(Data_Processing_1_rd),
    .Flags_Update_Mask(Data_Processing_1_flags_update_mask), .Opcode(Data_Processing_1_opcode));
  Flags_APSR flags_apsr_1 (
    .Update_Mask(or_1_out), .Flags_In(Flags), .Clk(Clk), .Rst(Reset), .Flags_Out(flags_apsr_1_flags_out));
  Load_Store Load_Store_1 (
    .Instruction(Inst), .Load(Load), .RAM_Addr(RAM_Addr), .Store(Store), .Stack_Pointer(Stack_Pointer_q),
    .Enable(Opcode_Decoder_1_load_store), .Rd(Load_Store_1_rd), .Rm(Load_Store_1_rm), .Clk(Clk),
    .Reset(Reset), .PC_Hold(Load_Store_1_pc_hold));
  Conditional Conditional_1 (
    .Enable(Opcode_Decoder_1_conditional), .Offset(Conditional_1_offset), .Instruction(Inst),
    .Verified(Conditional_1_verified), .N(flags_apsr_1_flags_out[3]), .Z(flags_apsr_1_flags_out[2]),
    .C(flags_apsr_1_flags_out[1]), .V(flags_apsr_1_flags_out[0]));
  SP_Address SP_Address_1 (
    .New_Stack_Pointer(SP_Address_1_new_stack_pointer), .Stack_Pointer(Stack_Pointer_q),
    .Enable(Opcode_Decoder_1_sp_address), .Instruction(Inst), .Write_Enable(SP_Address_1_write_enable));
  Subtractor subtractor_1 (.a(Conditional_1_offset), .b(8'h1), .out(subtractor_1_out));  // open: bin, bout
  and and_1 (DP_Shift, Opcode_Decoder_1_shift, ~Opcode_Decoder_1_data_processing);  // AND_Gate
  not not_1 (not_1_out, Load_Store_1_pc_hold);
  Counter counter_1 (
    .clr(Reset), .load(Conditional_1_verified), .up(1'b1), .count(not_1_out), .clk(Clk),
    .D(subtractor_1_out), .Q(PC));  // open: carry
  Multiplexer #(.enable("false")) multiplexer_1 (
    .in0(flags_apsr_1_flags_out[1]), .in1(Shift_Add_Sub_Mov_1_carry), .out(Carry), .sel(DP_Shift));
  assign ALU_Opcode = Shift_Add_Sub_Mov_1_alu_opcode | Data_Processing_1_opcode;  // OR_Gate or_2, 4 bits wide
  assign Rm = Shift_Add_Sub_Mov_1_rm | Data_Processing_1_rm | Load_Store_1_rm;  // OR_Gate or_3, 3 bits wide
  assign Rn = Shift_Add_Sub_Mov_1_rn | Data_Processing_1_rn;  // OR_Gate or_4, 3 bits wide
  assign Rd = Shift_Add_Sub_Mov_1_rd | Data_Processing_1_rd | Load_Store_1_rd;  // OR_Gate or_5, 3 bits wide

  // Notes on the sheet:
  //   Extract carry
  //   Extract Opcode
  //   IF Reg_Imm=1 THEN use shift value from register ELSE use shift value from Imm5
  //   Buffer flags for next instruction
  //   remove the last tick of the clock
endmodule

module Conditional (
  input  [15:0] Instruction,
  input  Enable,
  input  N,
  input  Z,
  input  C,
  input  V,
  output [7:0] Offset,
  output Verified
);

  wire conditional_check_1_out_9;
  wire [15:8] multiplexer_1_out;

  Multiplexer #(.width(16), .enable("false")) multiplexer_1 (
    .in0({16{1'b0}}), .in1(Instruction), .out({multiplexer_1_out, Offset}), .sel(Enable));
  Conditional_Check conditional_check_1 (
    .in_7(C), .in_6(Z), .in_5(N), .in_4(multiplexer_1_out[8]), .in_3(multiplexer_1_out[9]),
    .in_2(multiplexer_1_out[10]), .in_1(multiplexer_1_out[11]), .in_8(V), .out_9(conditional_check_1_out_9));
  assign Verified = Enable ? conditional_check_1_out_9 : 1'bz;  // Controlled_Buffer controlled_buffer_1
  Pull_Resistor pull_resistor_1 (.node(Verified));
endmodule

module Opcode_Decoder (
  input  [5:0] Opcode,
  output Shift,
  output Data_Processing,
  output Load_Store,
  output SP_Address,
  output Conditional
);

  wire and_3_out, and_4_out, nb0, nb1, nb2, nb3, nb4, nb5;

  not not_1 (nb0, Opcode[0]);
  not not_2 (nb1, Opcode[1]);
  not not_3 (nb2, Opcode[2]);
  not not_4 (nb3, Opcode[3]);
  not not_5 (nb4, Opcode[4]);
  not not_6 (nb5, Opcode[5]);
  and and_1 (Shift, nb5, nb4);
  and and_2 (Data_Processing, nb5, Opcode[4], nb3, nb2, nb1, nb0);
  and and_3 (and_3_out, nb5, Opcode[4], Opcode[3], nb2);
  and and_4 (and_4_out, Opcode[5], nb4, nb3, Opcode[2]);
  and and_5 (SP_Address, Opcode[5], nb4, Opcode[3], Opcode[2]);
  and and_6 (Conditional, Opcode[5], Opcode[4], nb3, Opcode[2]);
  or or_1 (Load_Store, and_3_out, and_4_out);

  // Other names for the same wires on the sheet: b0 = Opcode[0]; b1 = Opcode[1]; b2 = Opcode[2]; b3 = Opcode[3];
  //   b4 = Opcode[4]; b5 = Opcode[5]

  // Notes on the sheet:
  //   seems to be 0110 in the course but 1001 in some instructions
  //   Shift, add, sub, mov
  //   Load/Store
  //   SP Address
  //   Conditional branch
  //   Data Processing
endmodule

module Data_Processing (
  input  [15:0] Instructions,
  input  Enable,
  output [2:0] Rn,
  output [2:0] Rm,
  output [2:0] Rd,
  output [3:0] Flags_Update_Mask,
  output [3:0] Opcode
);

  wire and_1_out, and_2_out, not_1_out, not_2_out, not_3_out, or_1_out;
  wire [3:0] flags_data_proc_1_v;
  wire [15:10] Inst;

  Pull_Resistor pull_resistor_1 (.node({Inst, Opcode, Rm, Rd}));
  assign {Inst, Opcode, Rm, Rd} = Enable ? Instructions : 16'bz;  // Controlled_Buffer controlled_buffer_1
  not not_1 (not_1_out, Opcode[1]);
  not not_2 (not_2_out, Opcode[2]);
  and and_1 (and_1_out, Opcode[0], not_1_out, not_2_out, Opcode[3]);
  and and_2 (and_2_out, Opcode[0], Opcode[1], Opcode[2], Opcode[3]);
  Flags_Data_Proc flags_data_proc_1 (
    .C(flags_data_proc_1_v[1]), .Z(flags_data_proc_1_v[2]), .N(flags_data_proc_1_v[3]), .in_4(Opcode[0]),
    .in_3(Opcode[1]), .in_2(Opcode[2]), .in_1(Opcode[3]), .V(flags_data_proc_1_v[0]));
  or or_1 (or_1_out, and_1_out, and_2_out);
  Pull_Resistor pull_resistor_2 (.node(Flags_Update_Mask));
  assign Flags_Update_Mask = Enable ? flags_data_proc_1_v : 4'bz;  // Controlled_Buffer controlled_buffer_2
  assign Rn = not_3_out ? Rd : 3'bz;  // Controlled_Buffer controlled_buffer_3
  Pull_Resistor pull_resistor_3 (.node(Rn));
  not not_3 (not_3_out, or_1_out);

  // Other names for the same wires on the sheet: Inst[9:0] = {Opcode, Rm, Rd}; Rn_t[2:0] = Rd; Op[3:0] = Opcode

  // Notes on the sheet:
  //   Pull output low on Enable = 0
  //   Note 2: RSB instruction has Rn as 1st operand.
  //   MUL instruction has Rn as 1st operand and Rdm as 2nd operand
  //   For simplification purposes, Rm is used for 1st operand both here and in the ALU.
  //   Note: instructions that does not save the result will still have the second operand as the destination register, the ALU will copy the second register to the destination register
endmodule

module Shift_Add_Sub_Mov (
  input  [15:0] Instruction,
  input  Enable,
  output [2:0] Rn,
  output [4:0] Imm5,
  output [2:0] Rm,
  output [2:0] Rd,
  output Imm32_Enable,
  output [31:0] out_8,
  output [3:0] ALU_Opcode,
  output Carry,
  output [3:0] Flags_Update_Mask
);

  wire ADD, ADD_IMM, ADD_SUB, ADD_SUB_IMM, decode_operand_1_asr, decode_operand_1_lsl, decode_operand_1_lsr,
       i0, i1, i2, i3, i4, i5, i6, i7, i8, i9, i10, MOV, or_6_out, SHIFT, SUB, SUB_IMM;
  wire [1:0] or_4_out;
  wire [2:0] controlled_buffer_6_out;
  wire [3:0] flags_mask_1_v, opcode_instruction_1_b3;
  wire [15:11] Inst;
  wire [31:0] bit_extender_1_out, bit_extender_2_out, controlled_buffer_7_out, negator_1_out;

  Pull_Resistor pull_resistor_1 (.node({Inst, i10, i9, i8, i7, i6, i5, i4, i3, i2, i1, i0}));
  assign {Inst, i10, i9, i8, i7, i6, i5, i4, i3, i2, i1, i0} = Enable ? Instruction : 16'bz;  // Controlled_Buffer controlled_buffer_1
  Opcode_Instruction opcode_instruction_1 (
    .op0(i9), .op1(i10), .b0(opcode_instruction_1_b3[3]), .op2(Inst[11]), .b1(opcode_instruction_1_b3[2]),
    .op3(Inst[12]), .op4(Inst[13]), .b2(opcode_instruction_1_b3[1]), .b3(opcode_instruction_1_b3[0]));
  Decode_Operand decode_operand_1 (
    .LSL(decode_operand_1_lsl), .op0(i9), .op4(Inst[13]), .SUB(SUB), .LSR(decode_operand_1_lsr), .op1(i10),
    .op3(Inst[12]), .ADD(ADD), .ASR(decode_operand_1_asr), .op2(Inst[11]), .ADD_IMM(ADD_IMM),
    .SUB_IMM(SUB_IMM), .MOV(MOV));
  Pull_Resistor pull_resistor_2 (.node(ALU_Opcode));
  assign ALU_Opcode = Enable ? opcode_instruction_1_b3 : 4'bz;  // Controlled_Buffer controlled_buffer_2
  or or_1 (SHIFT, decode_operand_1_lsl, decode_operand_1_lsr, decode_operand_1_asr);
  or or_2 (ADD_SUB, ADD, SUB);
  or or_3 (ADD_SUB_IMM, ADD_IMM, SUB_IMM);
  // Probe on {i7, i6, i5, i4, i3, i2, i1, i0}
  assign bit_extender_1_out = {{24{1'b0}}, {i7, i6, i5, i4, i3, i2, i1, i0}};  // Bit_Extender bit_extender_1
  Negator #(.width(32)) negator_1 (.in(bit_extender_1_out), .out(negator_1_out));
  or or_4 (or_4_out[0], ADD, ADD_IMM);
  or or_5 (or_4_out[1], SUB, SUB_IMM);
  assign Rn = or_6_out ? {i5, i4, i3} : 3'bz;  // Controlled_Buffer controlled_buffer_3
  Pull_Resistor pull_resistor_3 (.node(Rn));
  or or_6 (or_6_out, SHIFT, ADD_SUB);
  assign Imm5 = SHIFT ? {i10, i9, i8, i7, i6} : 5'bz;  // Controlled_Buffer controlled_buffer_4
  Pull_Resistor pull_resistor_4 (.node(Imm5));
  assign Rm = ADD_SUB ? {i8, i7, i6} : 3'bz;  // Controlled_Buffer controlled_buffer_5
  Pull_Resistor pull_resistor_5 (.node(Rm));
  Multiplexer #(.width(3), .enable("false")) multiplexer_1 (
    .in0({i2, i1, i0}), .in1({i10, i9, i8}), .out(Rd), .sel(MOV));
  assign controlled_buffer_6_out = ADD_SUB_IMM ? {i8, i7, i6} : 3'bz;  // Controlled_Buffer controlled_buffer_6
  or or_7 (Imm32_Enable, ADD_SUB_IMM, MOV);
  assign controlled_buffer_7_out = MOV ? negator_1_out : 32'bz;  // Controlled_Buffer controlled_buffer_7
  Multiplexer #(.select(2), .enable("false")) multiplexer_2 (
    .in0(1'b0), .in1(1'b0), .in2(1'b1), .in3(1'b0), .out(Carry), .sel(or_4_out));
  // Probe on or_4_out
  Flags_Mask flags_mask_1 (
    .C(flags_mask_1_v[1]), .Add_Sub(ADD_SUB), .Move(MOV), .N(flags_mask_1_v[3]), .Shift(SHIFT),
    .Z(flags_mask_1_v[2]), .Imm(ADD_SUB_IMM), .V(flags_mask_1_v[0]));
  Pull_Resistor pull_resistor_6 (.node(controlled_buffer_6_out));
  assign bit_extender_2_out = {{29{1'b0}}, controlled_buffer_6_out};  // Bit_Extender bit_extender_2
  Pull_Resistor pull_resistor_7 (.node(controlled_buffer_7_out));
  assign Flags_Update_Mask = Enable ? flags_mask_1_v : 4'bz;  // Controlled_Buffer controlled_buffer_8
  Pull_Resistor pull_resistor_8 (.node(Flags_Update_Mask));
  // Probe on out_8
  assign out_8 = bit_extender_2_out | controlled_buffer_7_out;  // OR_Gate or_8, 32 bits wide

  // Other names for the same wires on the sheet: En = Enable; Imm8[7:0] = {i7, i6, i5, i4, i3, i2, i1, i0};
  //   Inst[10:0] = {i10, i9, i8, i7, i6, i5, i4, i3, i2, i1, i0}; Rd_t[2:0] = {i2, i1, i0}; Rn_t[2:0] = {i5, i4, i3};
  //   Imm3[2:0] = {i8, i7, i6}; Imm5_t[4:0] = {i10, i9, i8, i7, i6}; Rm_t[2:0] = {i8, i7, i6};
  //   Rdm[2:0] = {i10, i9, i8}

  // Notes on the sheet:
  //   Pull output low on Enable = 0
  //   Note 3: Imm32_Enable forces the use of the immediate for Rm register
  //   Note: ALU uses Rn register for shifts. Use Rn instead of Rm for shifts (immediate) here too
  //   Note 2: MOV uses RSB ALU opcode with Imm8 reversed so that it is copied to output register
  //   Enable carry for SUB since it is reversed in ALU
  //   ALU will use Imm32 instead of Rm
endmodule

module Load_Store (
  input  [15:0] Instruction,
  input  Enable,
  input  [31:0] Stack_Pointer,
  input  Clk,
  input  Reset,
  output Store,
  output Load,
  output PC_Hold,
  output [2:0] Rm,
  output [2:0] Rd,
  output [31:0] RAM_Addr
);

  wire and_1_out, controlled_buffer_1_out, d_ff_1_q, d_ff_1_qn;
  wire [2:0] controlled_buffer_2_out;
  wire [31:0] bit_extender_1_out;

  assign controlled_buffer_1_out = Enable ? Instruction[11] : 1'bz;  // Controlled_Buffer controlled_buffer_1
  assign bit_extender_1_out = {{24{1'b0}}, Instruction[7:0]};  // Bit_Extender bit_extender_1
  Pull_Resistor pull_resistor_1 (.node(controlled_buffer_1_out));
  Adder #(.width(32)) adder_1 (.a(bit_extender_1_out), .b(Stack_Pointer), .out(RAM_Addr));  // open: cin, cout
  and and_1 (and_1_out, d_ff_1_qn, controlled_buffer_1_out);
  D_Flip_Flop d_ff_1 (.D(and_1_out), .clk(Clk), .Q(d_ff_1_q), .Qn(d_ff_1_qn), .reset(Reset));  // open: preset
  assign controlled_buffer_2_out = Enable ? Instruction[10:8] : 3'bz;  // Controlled_Buffer controlled_buffer_2
  Pull_Resistor pull_resistor_2 (.node(Store));
  assign Store = Enable ? ~controlled_buffer_1_out : 1'bz;  // Controlled_Inverter controlled_inverter_1
  and and_2 (Load, controlled_buffer_1_out, d_ff_1_q);
  and and_3 (PC_Hold, d_ff_1_qn, controlled_buffer_1_out);
  Demultiplexer #(.width(3), .enable("false")) demultiplexer_1 (
    .out0(Rm), .out1(Rd), .in(controlled_buffer_2_out), .sel(controlled_buffer_1_out));
  Pull_Resistor pull_resistor_3 (.node(controlled_buffer_2_out));

  // Other names for the same wires on the sheet: En = Enable; Imm8[7:0] = Instruction[7:0];
  //   Rt[2:0] = Instruction[10:8]

  // Notes on the sheet:
  //   Delay load and hold PC for 1 cycle for the RAM to send out requested data 
endmodule

module SP_Address (
  input  [15:0] Instruction,
  input  [31:0] Stack_Pointer,
  input  Enable,
  output [31:0] New_Stack_Pointer,
  output Write_Enable
);

  wire comparator_1_eq, not_1_out;
  wire [15:0] controlled_buffer_1_out;
  wire [31:0] adder_1_out, bit_extender_1_out, pull_resistor_2_node, subtractor_1_out;

  // Probe on pull_resistor_2_node
  assign controlled_buffer_1_out = Enable ? Instruction : 16'bz;  // Controlled_Buffer controlled_buffer_1
  Pull_Resistor pull_resistor_1 (.node(controlled_buffer_1_out));
  Pull_Resistor pull_resistor_2 (.node(pull_resistor_2_node));
  assign pull_resistor_2_node = Enable ? Stack_Pointer : 32'bz;  // Controlled_Buffer controlled_buffer_2
  assign bit_extender_1_out = {{25{1'b0}}, controlled_buffer_1_out[6:0]};  // Bit_Extender bit_extender_1
  // Probe on bit_extender_1_out
  Subtractor #(.width(32)) subtractor_1 (
    .a(pull_resistor_2_node), .b(bit_extender_1_out), .out(subtractor_1_out));  // open: bin, bout
  Adder #(.width(32)) adder_1 (.a(pull_resistor_2_node), .b(bit_extender_1_out), .out(adder_1_out));  // open: cin, cout
  // Probe on New_Stack_Pointer
  Multiplexer #(.width(32), .enable("false")) multiplexer_1 (
    .in0(subtractor_1_out), .in1(adder_1_out), .out(New_Stack_Pointer), .sel(controlled_buffer_1_out[7]));
  not not_1 (not_1_out, comparator_1_eq);
  Comparator #(.width(32)) comparator_1 (
    .a(New_Stack_Pointer), .b(pull_resistor_2_node), .eq(comparator_1_eq));  // open: gt, lt
  and and_1 (Write_Enable, not_1_out, Enable);

  // Notes on the sheet:
  //   Pull output low on Enable = 0
endmodule

module Flags_APSR (
  input  [3:0] Update_Mask,
  input  [3:0] Flags_In,
  input  Clk,
  input  Rst,
  output [3:0] Flags_Out
);

  wire [3:0] and_1_out, and_2_out, not_1_out, or_1_out;

  assign not_1_out = ~Update_Mask;  // NOT_Gate not_1, 4 bits wide
  assign and_1_out = Flags_Out & not_1_out;  // AND_Gate and_1, 4 bits wide
  assign and_2_out = Update_Mask & Flags_In;  // AND_Gate and_2, 4 bits wide
  assign or_1_out = and_1_out | and_2_out;  // OR_Gate or_1, 4 bits wide
  Register #(.width(4)) register_1 (.D(or_1_out), .clk(Clk), .Q(Flags_Out), .clr(Rst));  // open: en
endmodule

module Decode_Operand (
  input  op0,
  input  op1,
  input  op2,
  input  op3,
  input  op4,
  output LSL,
  output LSR,
  output ASR,
  output ADD,
  output SUB,
  output ADD_IMM,
  output SUB_IMM,
  output MOV
);

  wire not_1_out, not_2_out, not_3_out, not_4_out, not_5_out, not_6_out, not_7_out, not_8_out, not_9_out,
       not_10_out, not_11_out, not_12_out, not_13_out, not_14_out, not_15_out, not_16_out, not_17_out;

  not not_1 (not_1_out, op2);
  not not_2 (not_2_out, op3);
  not not_3 (not_3_out, op4);
  not not_4 (not_4_out, op3);
  not not_5 (not_5_out, op4);
  not not_6 (not_6_out, op2);
  not not_7 (not_7_out, op4);
  not not_8 (not_8_out, op0);
  not not_9 (not_9_out, op1);
  not not_10 (not_10_out, op4);
  not not_11 (not_11_out, op1);
  not not_12 (not_12_out, op4);
  not not_13 (not_13_out, op0);
  not not_14 (not_14_out, op4);
  not not_15 (not_15_out, op4);
  not not_16 (not_16_out, op2);
  not not_17 (not_17_out, op3);
  and and_1 (LSL, not_1_out, not_2_out, not_3_out);
  and and_2 (LSR, op2, not_4_out, not_5_out);
  and and_3 (ASR, not_6_out, op3, not_7_out);
  and and_4 (ADD, not_8_out, not_9_out, op2, op3, not_10_out);
  and and_5 (SUB, op0, not_11_out, op2, op3, not_12_out);
  and and_6 (ADD_IMM, not_13_out, op1, op2, op3, not_14_out);
  and and_7 (SUB_IMM, op0, op1, op2, op3, not_15_out);
  and and_8 (MOV, not_16_out, not_17_out, op4);
endmodule

module Opcode_Instruction (
  input  op0,
  input  op1,
  input  op2,
  input  op3,
  input  op4,
  output b0,
  output b1,
  output b2,
  output b3
);

  wire and_2_out, and_3_out, and_4_out, and_5_out, and_6_out, and_7_out, and_8_out, and_9_out, not_1_out,
       not_2_out, not_3_out, not_4_out, not_5_out, not_6_out, not_7_out, not_8_out, not_9_out, not_10_out,
       not_11_out, not_12_out, not_13_out, not_14_out;

  not not_1 (not_1_out, op0);
  not not_2 (not_2_out, op1);
  not not_3 (not_3_out, op2);
  not not_4 (not_4_out, op3);
  not not_5 (not_5_out, op3);
  not not_6 (not_6_out, op4);
  not not_7 (not_7_out, op3);
  not not_8 (not_8_out, op3);
  not not_9 (not_9_out, op3);
  not not_10 (not_10_out, op0);
  not not_11 (not_11_out, op1);
  not not_12 (not_12_out, op3);
  not not_13 (not_13_out, op0);
  not not_14 (not_14_out, op3);
  and and_1 (b0, not_1_out, not_2_out, not_3_out, not_4_out, op4);
  and and_2 (and_2_out, not_5_out, not_6_out);
  and and_3 (and_3_out, op2, not_7_out);
  and and_4 (and_4_out, op1, not_8_out);
  and and_5 (and_5_out, op0, not_9_out);
  and and_6 (and_6_out, op0, op2);
  and and_7 (and_7_out, not_10_out, not_11_out, not_12_out, op4);
  and and_8 (and_8_out, not_13_out, op2);
  and and_9 (and_9_out, op2, not_14_out);
  or or_1 (b2, and_2_out, and_3_out, and_4_out, and_5_out, and_6_out);
  or or_2 (b3, and_7_out, and_8_out, and_9_out);

  assign b1 = op3;
endmodule

module Flags_Mask (
  input  Shift,
  input  Add_Sub,
  input  Imm,
  input  Move,
  output N,
  output Z,
  output C,
  output V
);

  wire and_1_out, and_2_out, and_3_out, and_4_out, and_5_out, and_6_out, and_7_out, and_8_out, and_9_out,
       and_10_out, and_11_out, and_12_out, and_13_out, not_1_out, not_2_out, not_3_out, not_4_out, not_5_out,
       not_6_out, not_7_out, not_8_out, not_9_out, not_10_out, not_11_out, not_12_out, not_13_out,
       not_14_out, not_15_out, not_16_out, not_17_out, not_18_out, not_19_out, not_20_out, not_21_out,
       not_22_out, not_23_out, not_24_out, not_25_out, not_26_out, not_27_out, not_28_out, not_29_out,
       not_30_out, not_31_out, not_32_out, not_33_out, not_34_out, not_35_out, not_36_out, not_37_out,
       not_38_out, not_39_out;

  not not_1 (not_1_out, Shift);
  not not_2 (not_2_out, Add_Sub);
  not not_3 (not_3_out, Imm);
  not not_4 (not_4_out, Shift);
  not not_5 (not_5_out, Add_Sub);
  not not_6 (not_6_out, Move);
  not not_7 (not_7_out, Shift);
  not not_8 (not_8_out, Imm);
  not not_9 (not_9_out, Move);
  not not_10 (not_10_out, Add_Sub);
  not not_11 (not_11_out, Imm);
  not not_12 (not_12_out, Move);
  not not_13 (not_13_out, Shift);
  not not_14 (not_14_out, Add_Sub);
  not not_15 (not_15_out, Imm);
  not not_16 (not_16_out, Shift);
  not not_17 (not_17_out, Add_Sub);
  not not_18 (not_18_out, Move);
  not not_19 (not_19_out, Shift);
  not not_20 (not_20_out, Imm);
  not not_21 (not_21_out, Move);
  not not_22 (not_22_out, Add_Sub);
  not not_23 (not_23_out, Imm);
  not not_24 (not_24_out, Move);
  not not_25 (not_25_out, Shift);
  not not_26 (not_26_out, Add_Sub);
  not not_27 (not_27_out, Move);
  not not_28 (not_28_out, Shift);
  not not_29 (not_29_out, Imm);
  not not_30 (not_30_out, Move);
  not not_31 (not_31_out, Add_Sub);
  not not_32 (not_32_out, Imm);
  not not_33 (not_33_out, Move);
  not not_34 (not_34_out, Shift);
  not not_35 (not_35_out, Add_Sub);
  not not_36 (not_36_out, Move);
  not not_37 (not_37_out, Shift);
  not not_38 (not_38_out, Imm);
  not not_39 (not_39_out, Move);
  and and_1 (and_1_out, not_1_out, not_2_out, not_3_out, Move);
  and and_2 (and_2_out, not_4_out, not_5_out, Imm, not_6_out);
  and and_3 (and_3_out, not_7_out, Add_Sub, not_8_out, not_9_out);
  and and_4 (and_4_out, Shift, not_10_out, not_11_out, not_12_out);
  and and_5 (and_5_out, not_13_out, not_14_out, not_15_out, Move);
  and and_6 (and_6_out, not_16_out, not_17_out, Imm, not_18_out);
  and and_7 (and_7_out, not_19_out, Add_Sub, not_20_out, not_21_out);
  and and_8 (and_8_out, Shift, not_22_out, not_23_out, not_24_out);
  and and_9 (and_9_out, not_25_out, not_26_out, Imm, not_27_out);
  or or_1 (C, and_9_out, and_10_out, and_11_out);
  and and_10 (and_10_out, not_28_out, Add_Sub, not_29_out, not_30_out);
  and and_11 (and_11_out, Shift, not_31_out, not_32_out, not_33_out);
  and and_12 (and_12_out, not_34_out, not_35_out, Imm, not_36_out);
  or or_2 (V, and_12_out, and_13_out);
  and and_13 (and_13_out, not_37_out, Add_Sub, not_38_out, not_39_out);
  or or_3 (N, and_1_out, and_2_out, and_3_out, and_4_out);
  or or_4 (Z, and_5_out, and_6_out, and_7_out, and_8_out);
endmodule

module Flags_Data_Proc (
  input  in_1,
  input  in_2,
  input  in_3,
  input  in_4,
  output N,
  output Z,
  output C,
  output V
);

  wire and_1_out, and_2_out, and_3_out, and_4_out, nand_1_out, nand_2_out, nand_3_out, not_1_out, not_2_out,
       not_3_out, not_4_out, not_5_out, not_6_out, not_7_out, not_8_out, not_9_out, not_10_out, not_11_out;

  not not_1 (not_1_out, in_1);
  not not_2 (not_2_out, in_2);
  not not_3 (not_3_out, in_4);
  not not_4 (not_4_out, in_3);
  not not_5 (not_5_out, in_1);
  not not_6 (not_6_out, in_3);
  not not_7 (not_7_out, in_1);
  not not_8 (not_8_out, in_4);
  not not_9 (not_9_out, in_2);
  not not_10 (not_10_out, in_3);
  not not_11 (not_11_out, in_2);
  nand nand_1 (nand_1_out, not_1_out, in_2, in_3, in_4);
  nand nand_2 (nand_2_out, in_1, not_2_out, in_3, not_3_out);
  nand nand_3 (nand_3_out, in_1, in_2, not_4_out, in_4);
  and and_1 (and_1_out, not_5_out, in_2, not_6_out, in_4);
  and and_2 (and_2_out, not_7_out, in_2, in_3, not_8_out);
  and and_3 (and_3_out, in_1, not_9_out, not_10_out, in_4);
  and and_4 (and_4_out, in_1, not_11_out, in_3, in_4);
  and and_5 (C, nand_1_out, nand_2_out, nand_3_out);
  or or_1 (V, and_1_out, and_2_out, and_3_out, and_4_out);

  assign N = 1'b1;
  assign Z = 1'b1;
endmodule

module Conditional_Check (
  input  in_1,
  input  in_2,
  input  in_3,
  input  in_4,
  input  in_5,
  input  in_6,
  input  in_7,
  input  in_8,
  output out_9
);

  wire and_1_out, and_2_out, and_3_out, and_4_out, and_5_out, and_6_out, and_7_out, and_8_out, and_9_out,
       and_10_out, and_11_out, and_12_out, and_13_out, and_14_out, and_15_out, and_16_out, and_17_out,
       and_18_out, and_19_out, and_20_out, and_21_out, and_22_out, and_23_out, not_1_out, not_2_out,
       not_3_out, not_4_out, not_5_out, not_6_out, not_7_out, not_8_out, not_9_out, not_10_out, not_11_out,
       not_12_out, not_13_out, not_14_out, not_15_out, not_16_out, not_17_out, not_18_out, not_19_out,
       not_20_out, not_21_out, not_22_out, not_23_out, not_24_out, not_25_out, not_26_out, not_27_out,
       not_28_out, not_29_out, not_30_out, not_31_out, not_32_out, not_33_out, not_34_out, not_35_out,
       not_36_out, not_37_out, not_38_out, not_39_out, not_40_out, not_41_out, not_42_out, not_43_out,
       not_44_out, not_45_out, not_46_out, not_47_out, or_1_out, or_2_out, or_3_out, or_4_out;

  not not_1 (not_1_out, in_5);
  not not_2 (not_2_out, in_8);
  not not_3 (not_3_out, in_8);
  not not_4 (not_4_out, in_5);
  and and_1 (and_1_out, in_5, in_8);
  not not_5 (not_5_out, in_5);
  and and_2 (and_2_out, not_5_out, not_6_out);
  not not_6 (not_6_out, in_8);
  and and_3 (and_3_out, in_5, not_7_out);
  not not_7 (not_7_out, in_8);
  not not_8 (not_8_out, in_5);
  and and_4 (and_4_out, not_8_out, in_8);
  not not_9 (not_9_out, in_1);
  not not_10 (not_10_out, in_2);
  not not_11 (not_11_out, in_3);
  not not_12 (not_12_out, in_4);
  not not_13 (not_13_out, in_1);
  not not_14 (not_14_out, in_2);
  not not_15 (not_15_out, in_3);
  not not_16 (not_16_out, in_6);
  not not_17 (not_17_out, in_1);
  not not_18 (not_18_out, in_2);
  not not_19 (not_19_out, in_4);
  not not_20 (not_20_out, in_1);
  not not_21 (not_21_out, in_2);
  not not_22 (not_22_out, in_7);
  not not_23 (not_23_out, in_1);
  not not_24 (not_24_out, in_3);
  not not_25 (not_25_out, in_4);
  not not_26 (not_26_out, in_1);
  not not_27 (not_27_out, in_3);
  not not_28 (not_28_out, in_5);
  not not_29 (not_29_out, in_1);
  not not_30 (not_30_out, in_4);
  not not_31 (not_31_out, in_1);
  not not_32 (not_32_out, in_8);
  not not_33 (not_33_out, in_2);
  not not_34 (not_34_out, in_3);
  not not_35 (not_35_out, in_4);
  not not_36 (not_36_out, in_8);
  not not_37 (not_37_out, in_2);
  not not_38 (not_38_out, in_3);
  not not_39 (not_39_out, in_7);
  not not_40 (not_40_out, in_2);
  not not_41 (not_41_out, in_4);
  and and_5 (and_5_out, in_5, in_8);
  or or_1 (or_1_out, and_5_out, and_6_out);
  and and_6 (and_6_out, not_1_out, not_2_out);
  not not_42 (not_42_out, in_2);
  and and_7 (and_7_out, in_5, not_3_out);
  or or_2 (or_2_out, and_7_out, and_8_out);
  and and_8 (and_8_out, not_4_out, in_8);
  not not_43 (not_43_out, in_3);
  not not_44 (not_44_out, in_4);
  not not_45 (not_45_out, in_6);
  or or_3 (or_3_out, and_1_out, and_2_out);
  not not_46 (not_46_out, in_3);
  or or_4 (or_4_out, and_3_out, and_4_out);
  not not_47 (not_47_out, in_4);
  and and_9 (and_9_out, not_9_out, not_10_out, not_11_out, not_12_out, in_6);
  and and_10 (and_10_out, not_13_out, not_14_out, not_15_out, in_4, not_16_out);
  and and_11 (and_11_out, not_17_out, not_18_out, in_3, not_19_out, in_7);
  and and_12 (and_12_out, not_20_out, not_21_out, in_3, in_4, not_22_out);
  and and_13 (and_13_out, not_23_out, in_2, not_24_out, not_25_out, in_5);
  and and_14 (and_14_out, not_26_out, in_2, not_27_out, in_4, not_28_out);
  and and_15 (and_15_out, not_29_out, in_2, in_3, not_30_out, in_8);
  and and_16 (and_16_out, not_31_out, in_2, in_3, in_4, not_32_out);
  and and_17 (and_17_out, in_1, not_33_out, not_34_out, not_35_out, in_7, not_36_out);
  and and_18 (and_18_out, in_1, not_37_out, not_38_out, in_4, not_39_out, in_6);
  and and_19 (and_19_out, in_1, not_40_out, in_3, not_41_out, or_1_out);
  and and_20 (and_20_out, in_1, not_42_out, in_3, in_4, or_2_out);
  and and_21 (and_21_out, in_1, in_2, not_43_out, not_44_out, not_45_out, or_3_out);
  and and_22 (and_22_out, in_1, in_2, not_46_out, in_4, in_6, or_4_out);
  and and_23 (and_23_out, in_1, in_2, in_3, not_47_out);
  or or_5 (out_9, and_9_out, and_10_out, and_11_out, and_12_out, and_13_out, and_14_out, and_15_out, and_16_out, and_17_out, and_18_out, and_19_out, and_20_out, and_21_out, and_22_out, and_23_out);
endmodule

module Test_Flags_APSR (
  input  [3:0] Update_Mask,
  input  [3:0] Flags_In,
  input  Rst,
  input  in_4,
  input  [15:0] in_5,
  input  in_6,
  input  in_7,
  input  in_8,
  input  in_9,
  output [3:0] Flags_out
);

  wire clk_out, comparator_1_eq, conditional_1_verified;
  wire [7:0] conditional_1_offset;

  Clock clk (.out(clk_out));
  Clock sysclk ();  // open: out
  // Probe on conditional_1_offset
  Conditional conditional_1 (
    .Enable(in_4), .Offset(conditional_1_offset), .Instruction(in_5), .Verified(conditional_1_verified),
    .N(in_6), .Z(in_7), .C(in_8), .V(in_9));
  Flags_APSR flags_apsr_1 (
    .Update_Mask(Update_Mask), .Flags_In(Flags_In), .Clk(clk_out), .Rst(Rst), .Flags_Out(Flags_out));
  LED led_1 (.in(comparator_1_eq));
  Comparator comparator_1 (.a(conditional_1_offset), .b(8'h7), .eq(comparator_1_eq));  // open: gt, lt
  LED led_2 (.in(conditional_1_verified));

  // Notes on the sheet:
  //   Permet de générer le chronogramme
  //   code : 1001 - LS - Inférieur ou égal (non signé) - C == 0 & Z == 1
endmodule

module Test_Load_Store (
  input  [15:0] Instruction,
  input  En,
  input  [31:0] Stack_Pointer,
  input  Rst,
  output [2:0] Rm,
  output [2:0] Rd,
  output [31:0] RAM_Addr,
  output Load,
  output Store,
  output PC_Hold
);

  wire clk_out;

  Clock clk (.out(clk_out));
  Clock sysclk ();  // open: out
  Load_Store load_store_1 (
    .Instruction(Instruction), .Load(Load), .RAM_Addr(RAM_Addr), .Store(Store),
    .Stack_Pointer(Stack_Pointer), .Enable(En), .Rd(Rd), .Rm(Rm), .Clk(clk_out), .Reset(Rst),
    .PC_Hold(PC_Hold));

  // Notes on the sheet:
  //   Permet de générer le chronogramme
endmodule

module Test_SP_Address (
);

  wire comparator_1_eq, comparator_2_eq, comparator_3_eq, not_1_out, sp_address_1_write_enable,
       sp_address_2_write_enable, sp_address_3_write_enable;
  wire [31:0] sp_address_1_new_stack_pointer, sp_address_2_new_stack_pointer, sp_address_3_new_stack_pointer;

  SP_Address sp_address_1 (
    .New_Stack_Pointer(sp_address_1_new_stack_pointer), .Stack_Pointer(32'hf), .Enable(1'b1),
    .Instruction(16'hb00f), .Write_Enable(sp_address_1_write_enable));
  SP_Address sp_address_2 (
    .New_Stack_Pointer(sp_address_2_new_stack_pointer), .Stack_Pointer(32'hf), .Enable(1'b1),
    .Instruction(16'hb08f), .Write_Enable(sp_address_2_write_enable));
  SP_Address sp_address_3 (
    .New_Stack_Pointer(sp_address_3_new_stack_pointer), .Stack_Pointer(32'hf), .Enable(1'b0),
    .Instruction(16'hb00f), .Write_Enable(sp_address_3_write_enable));
  // Probe on sp_address_1_new_stack_pointer
  // Probe on sp_address_2_new_stack_pointer
  // Probe on sp_address_3_new_stack_pointer
  not not_1 (not_1_out, sp_address_3_write_enable);
  Comparator #(.width(32)) comparator_1 (
    .a(sp_address_1_new_stack_pointer), .b({32{1'b0}}), .eq(comparator_1_eq));  // open: gt, lt
  LED led_1 (.in(comparator_1_eq));
  LED led_2 (.in(sp_address_1_write_enable));
  LED led_3 (.in(comparator_2_eq));
  Comparator #(.width(32)) comparator_2 (
    .a(sp_address_2_new_stack_pointer), .b(32'h1e), .eq(comparator_2_eq));  // open: gt, lt
  LED led_4 (.in(sp_address_2_write_enable));
  Comparator #(.width(32)) comparator_3 (
    .a(sp_address_3_new_stack_pointer), .b({32{1'b0}}), .eq(comparator_3_eq));  // open: gt, lt
  LED led_5 (.in(comparator_3_eq));
  LED led_6 (.in(not_1_out));

  // Notes on the sheet:
  //   Test with negative gate
  //   Test with positive gate
  //   Test when disabled
  //   vert : VALIDE   rouge : ERREUR
endmodule

module Test_Conditional (
);

  wire comparator_1_eq, comparator_2_eq, comparator_3_eq, comparator_4_eq, comparator_5_eq, comparator_6_eq,
       comparator_7_eq, comparator_8_eq, comparator_9_eq, comparator_10_eq, comparator_11_eq,
       comparator_12_eq, comparator_13_eq, comparator_14_eq, comparator_15_eq, conditional_1_verified,
       conditional_2_verified, conditional_3_verified, conditional_4_verified, conditional_5_verified,
       conditional_6_verified, conditional_7_verified, conditional_8_verified, conditional_9_verified,
       conditional_10_verified, conditional_11_verified, conditional_12_verified, conditional_13_verified,
       conditional_14_verified, conditional_15_verified;
  wire [7:0] conditional_1_offset, conditional_2_offset, conditional_3_offset, conditional_4_offset,
       conditional_5_offset, conditional_6_offset, conditional_7_offset, conditional_8_offset,
       conditional_9_offset, conditional_10_offset, conditional_11_offset, conditional_12_offset,
       conditional_13_offset, conditional_14_offset, conditional_15_offset;

  // Probe on conditional_1_offset
  Conditional conditional_1 (
    .Enable(1'b1), .Offset(conditional_1_offset), .Instruction(16'hd007), .Verified(conditional_1_verified),
    .N(1'b0), .Z(1'b1), .C(1'b0), .V(1'b1));
  // Probe on conditional_2_offset
  Conditional conditional_2 (
    .Enable(1'b1), .Offset(conditional_2_offset), .Instruction(16'hd107), .Verified(conditional_2_verified),
    .N(1'b0), .Z(1'b0), .C(1'b0), .V(1'b0));
  // Probe on conditional_3_offset
  Conditional conditional_3 (
    .Enable(1'b1), .Offset(conditional_3_offset), .Instruction(16'hd207), .Verified(conditional_3_verified),
    .N(1'b0), .Z(1'b0), .C(1'b1), .V(1'b0));
  // Probe on conditional_4_offset
  Conditional conditional_4 (
    .Enable(1'b1), .Offset(conditional_4_offset), .Instruction(16'hd307), .Verified(conditional_4_verified),
    .N(1'b0), .Z(1'b1), .C(1'b0), .V(1'b1));
  // Probe on conditional_5_offset
  Conditional conditional_5 (
    .Enable(1'b1), .Offset(conditional_5_offset), .Instruction(16'hd407), .Verified(conditional_5_verified),
    .N(1'b1), .Z(1'b0), .C(1'b0), .V(1'b0));
  // Probe on conditional_6_offset
  Conditional conditional_6 (
    .Enable(1'b1), .Offset(conditional_6_offset), .Instruction(16'hd507), .Verified(conditional_6_verified),
    .N(1'b0), .Z(1'b1), .C(1'b0), .V(1'b0));
  // Probe on conditional_7_offset
  Conditional conditional_7 (
    .Enable(1'b1), .Offset(conditional_7_offset), .Instruction(16'hd607), .Verified(conditional_7_verified),
    .N(1'b0), .Z(1'b0), .C(1'b0), .V(1'b1));
  // Probe on conditional_8_offset
  Conditional conditional_8 (
    .Enable(1'b1), .Offset(conditional_8_offset), .Instruction(16'hd707), .Verified(conditional_8_verified),
    .N(1'b0), .Z(1'b0), .C(1'b1), .V(1'b0));
  // Probe on conditional_9_offset
  Conditional conditional_9 (
    .Enable(1'b1), .Offset(conditional_9_offset), .Instruction(16'hd807), .Verified(conditional_9_verified),
    .N(1'b0), .Z(1'b0), .C(1'b1), .V(1'b0));
  // Probe on conditional_10_offset
  Conditional conditional_10 (
    .Enable(1'b1), .Offset(conditional_10_offset), .Instruction(16'hd907),
    .Verified(conditional_10_verified), .N(1'b0), .Z(1'b1), .C(1'b0), .V(1'b0));
  // Probe on conditional_11_offset
  Conditional conditional_11 (
    .Enable(1'b1), .Offset(conditional_11_offset), .Instruction(16'hda07),
    .Verified(conditional_11_verified), .N(1'b0), .Z(1'b0), .C(1'b1), .V(1'b0));
  // Probe on conditional_12_offset
  Conditional conditional_12 (
    .Enable(1'b1), .Offset(conditional_12_offset), .Instruction(16'hdb07),
    .Verified(conditional_12_verified), .N(1'b1), .Z(1'b0), .C(1'b0), .V(1'b0));
  // Probe on conditional_13_offset
  Conditional conditional_13 (
    .Enable(1'b1), .Offset(conditional_13_offset), .Instruction(16'hdc07),
    .Verified(conditional_13_verified), .N(1'b1), .Z(1'b0), .C(1'b1), .V(1'b1));
  // Probe on conditional_14_offset
  Conditional conditional_14 (
    .Enable(1'b1), .Offset(conditional_14_offset), .Instruction(16'hdd07),
    .Verified(conditional_14_verified), .N(1'b0), .Z(1'b1), .C(1'b1), .V(1'b1));
  // Probe on conditional_15_offset
  Conditional conditional_15 (
    .Enable(1'b1), .Offset(conditional_15_offset), .Instruction(16'hde07),
    .Verified(conditional_15_verified), .N(1'b1), .Z(1'b1), .C(1'b1), .V(1'b1));
  Comparator comparator_1 (.a(conditional_1_offset), .b(8'h7), .eq(comparator_1_eq));  // open: gt, lt
  LED led_1 (.in(comparator_1_eq));
  LED led_2 (.in(conditional_1_verified));
  Comparator comparator_2 (.a(conditional_2_offset), .b(8'h7), .eq(comparator_2_eq));  // open: gt, lt
  LED led_3 (.in(comparator_2_eq));
  LED led_4 (.in(conditional_2_verified));
  LED led_5 (.in(comparator_3_eq));
  Comparator comparator_3 (.a(conditional_3_offset), .b(8'h7), .eq(comparator_3_eq));  // open: gt, lt
  LED led_6 (.in(conditional_3_verified));
  LED led_7 (.in(comparator_4_eq));
  Comparator comparator_4 (.a(conditional_4_offset), .b(8'h7), .eq(comparator_4_eq));  // open: gt, lt
  LED led_8 (.in(conditional_4_verified));
  Comparator comparator_5 (.a(conditional_5_offset), .b(8'h7), .eq(comparator_5_eq));  // open: gt, lt
  LED led_9 (.in(comparator_5_eq));
  LED led_10 (.in(conditional_5_verified));
  Comparator comparator_6 (.a(conditional_6_offset), .b(8'h7), .eq(comparator_6_eq));  // open: gt, lt
  LED led_11 (.in(comparator_6_eq));
  LED led_12 (.in(conditional_6_verified));
  LED led_13 (.in(comparator_7_eq));
  Comparator comparator_7 (.a(conditional_7_offset), .b(8'h7), .eq(comparator_7_eq));  // open: gt, lt
  LED led_14 (.in(conditional_7_verified));
  LED led_15 (.in(comparator_8_eq));
  Comparator comparator_8 (.a(conditional_8_offset), .b(8'h7), .eq(comparator_8_eq));  // open: gt, lt
  LED led_16 (.in(conditional_8_verified));
  LED led_17 (.in(comparator_9_eq));
  Comparator comparator_9 (.a(conditional_9_offset), .b(8'h7), .eq(comparator_9_eq));  // open: gt, lt
  LED led_18 (.in(conditional_9_verified));
  Comparator comparator_10 (.a(conditional_10_offset), .b(8'h7), .eq(comparator_10_eq));  // open: gt, lt
  LED led_19 (.in(comparator_10_eq));
  LED led_20 (.in(conditional_10_verified));
  Comparator comparator_11 (.a(conditional_11_offset), .b(8'h7), .eq(comparator_11_eq));  // open: gt, lt
  LED led_21 (.in(comparator_11_eq));
  LED led_22 (.in(conditional_11_verified));
  LED led_23 (.in(comparator_12_eq));
  Comparator comparator_12 (.a(conditional_12_offset), .b(8'h7), .eq(comparator_12_eq));  // open: gt, lt
  LED led_24 (.in(conditional_12_verified));
  LED led_25 (.in(comparator_13_eq));
  Comparator comparator_13 (.a(conditional_13_offset), .b(8'h7), .eq(comparator_13_eq));  // open: gt, lt
  LED led_26 (.in(conditional_13_verified));
  LED led_27 (.in(comparator_14_eq));
  Comparator comparator_14 (.a(conditional_14_offset), .b(8'h7), .eq(comparator_14_eq));  // open: gt, lt
  LED led_28 (.in(conditional_14_verified));
  LED led_29 (.in(comparator_15_eq));
  Comparator comparator_15 (.a(conditional_15_offset), .b(8'h7), .eq(comparator_15_eq));  // open: gt, lt
  LED led_30 (.in(conditional_15_verified));

  // Notes on the sheet:
  //   code : 0000 - EQ - Egalité - Z == 1
  //   code : 0001 - NE - Différence - Z == 0
  //   code : 0010 - CS - Retenue - C == 1
  //   code : 0011 - CC - Pas de retenue - C == 0
  //   code : 0100 - MI - Négatif - N == 1
  //   code : 0101 - PL - Positif ou nul - N == 0
  //   N : Résultat négatif, égal au bit de pods fort au résultat
  //   Z : Résultat nul, égal à 1 si le résultat est 0
  //   code : 0110 - VS - Dépassage de capacité - V == 1
  //   code : 0111 - VC - Pas de dépassage de capacité - V == 0
  //   code : 1000 - HI - Supérieur (non signé) - C == 1 & Z == 0
  //   code : 1001 - LS - Inférieur ou égal (non signé) - C == 0 & Z == 1
  //   code : 1010 - GE - Supérieur ou égal (signé) - N == V
  //   code : 1011 - LT - Inférieur (signé) - N != V
  //   code : 1100 - GT - Supérieur (signé) - Z == 0 & N == V
  //   code : 1101 - LE - Inférieur ou égal (signé) - Z == 1 & N != V
  //   code : 1110 - AL - Toujours vrai
  //   C : Retenue
  //   V : Dépassement de capacité
  //   vert : VALIDE   rouge : ERREUR
endmodule

module Offset (
  input  [7:0] Offset_in,
  input  [7:0] Counter,
  output [7:0] Offset_out
);

  wire comparator_1_eq, comparator_1_gt, down, up;
  wire [7:0] adder_1_out, controlled_buffer_1_out, controlled_buffer_2_out, subtractor_1_out,
       subtractor_2_out;

  Subtractor subtractor_1 (.a(Offset_in), .b(Counter), .out(subtractor_1_out));  // open: bin, bout
  Comparator comparator_1 (.a(subtractor_1_out), .b({8{1'b0}}), .gt(comparator_1_gt), .eq(comparator_1_eq), .lt(down));
  or or_1 (up, comparator_1_gt, comparator_1_eq);
  Adder adder_1 (.a(8'h3), .b(Offset_in), .out(adder_1_out), .cin(1'b0));  // open: cout
  Subtractor subtractor_2 (.a(Counter), .b(adder_1_out), .out(subtractor_2_out), .bin(1'b1));  // open: bout
  assign controlled_buffer_1_out = down ? subtractor_2_out : 8'bz;  // Controlled_Buffer controlled_buffer_1
  assign controlled_buffer_2_out = up ? Offset_in : 8'bz;  // Controlled_Buffer controlled_buffer_2
  Pull_Resistor pull_resistor_1 (.node(controlled_buffer_1_out));
  Pull_Resistor pull_resistor_2 (.node(controlled_buffer_2_out));
  assign Offset_out = controlled_buffer_1_out | controlled_buffer_2_out;  // OR_Gate or_2, 8 bits wide

  // Notes on the sheet:
  //   Add 3 to offset because ARM pre-increments PC
  //   and does an additionnal prefect operation
endmodule
