// Logisim project Machine.circ as structural Verilog: 2 circuits, main circuit main
module main (
  input  GPIO_A1,
  input  GPIO_A3,
  input  GPIO_A5,
  input  GPIO_A7,
  input  GPIO_A9,
  input  GPIO_A11,
  input  GPIO_A13,
  input  GPIO_A15,
  input  GPIO_A17,
  input  GPIO_A19,
  input  GPIO_A21,
  input  GPIO_A23,
  input  GPIO_A25,
  input  GPIO_A27,
  input  GPIO_A29,
  input  GPIO_A31,
  input  GPIO_A33,
  input  GPIO_A35,
  input  GPIO_B1,
  input  GPIO_B3,
  input  GPIO_B5,
  input  GPIO_B7,
  input  GPIO_B9,
  input  GPIO_B11,
  input  GPIO_B13,
  input  GPIO_B15,
  input  GPIO_B17,
  input  GPIO_B19,
  input  GPIO_B21,
  input  GPIO_B23,
  input  GPIO_B25,
  input  GPIO_B27,
  input  GPIO_B29,
  input  GPIO_B31,
  input  GPIO_B33,
  input  GPIO_B35,
  output GPIO_A2,
  output GPIO_A4,
  output GPIO_A6,
  output GPIO_A8,
  output GPIO_A10,
  output GPIO_A12,
  output GPIO_A14,
  output GPIO_A16,
  output GPIO_A18,
  output GPIO_A20,
  output GPIO_A22,
  output GPIO_A24,
  output GPIO_A26,
  output GPIO_A28,
  output GPIO_A30,
  output GPIO_A32,
  output GPIO_A34,
  output GPIO_A36,
  output GPIO_B2,
  output GPIO_B4,
  output GPIO_B6,
  output GPIO_B8,
  output GPIO_B10,
  output GPIO_B12,
  output GPIO_B14,
  output GPIO_B16,
  output GPIO_B18,
  output GPIO_B20,
  output GPIO_B22,
  output GPIO_B24,
  output GPIO_B26,
  output GPIO_B28,
  output GPIO_B30,
  output GPIO_B32,
  output GPIO_B34,
  output GPIO_B36
);

  wire Clk, Clk_Button_out, CPU_1_store, Rst, Rst_Button_out;
  wire [4:0] adder_1_out, register_1_q;
  wire [7:0] RAM_Addr, ROM_Addr;
  wire [15:0] ROMa_data;
  wire [31:0] CPU_1_r0, CPU_1_r1, CPU_1_r2, CPU_1_r3, CPU_1_r4, CPU_1_r5, CPU_1_r6, CPU_1_r7, CPU_1_ram_out,
       RAMa_dout;
  wire [31:8] CPU_1_ram_addr;

  RAM #(.dataWidth(32), .databus("bibus")) RAMa (
    .addr(RAM_Addr), .we(CPU_1_store), .oe(1'b1), .clk(Clk), .din(CPU_1_ram_out), .dout(RAMa_dout));
  Clock clock_1 (.out(Clk));
  LED A0 (.in(RAMa_dout[0]));
  LED A1 (.in(RAMa_dout[1]));
  LED A2 (.in(RAMa_dout[2]));
  ROM #(.dataWidth(16)) ROMa (.addr(ROM_Addr), .data(ROMa_data));
  Button Clk_Button (.out(Clk_Button_out));
  Button Rst_Button (.out(Rst_Button_out));
  LED A3 (.in(RAMa_dout[3]));
  LED A4 (.in(RAMa_dout[4]));
  LED A5 (.in(RAMa_dout[5]));
  LED A6 (.in(RAMa_dout[6]));
  LED A7 (.in(RAMa_dout[7]));
  LED L0 (.in(CPU_1_r0[0]));
  // Probe on CPU_1_r1
  // Probe on CPU_1_r0
  LED L3 (.in(CPU_1_r0[3]));
  LED L1 (.in(CPU_1_r0[1]));
  LED L2 (.in(CPU_1_r0[2]));
  // Probe on CPU_1_r3
  // Probe on CPU_1_r2
  // Probe on CPU_1_r5
  // Probe on CPU_1_r4
  LED L4 (.in(CPU_1_r0[4]));
  LED L5 (.in(CPU_1_r0[5]));
  // Probe on CPU_1_r7
  // Probe on CPU_1_r6
  CPU CPU_1 (
    .ROM_Addr(ROM_Addr), .RAM_In(RAMa_dout), .R3(CPU_1_r3), .R7(CPU_1_r7), .R2(CPU_1_r2), .R6(CPU_1_r6),
    .RAM_Addr({CPU_1_ram_addr, RAM_Addr}), .R5(CPU_1_r5), .ROM_In(ROMa_data), .R0(CPU_1_r0), .R4(CPU_1_r4),
    .Clk(Clk), .RAM_Out(CPU_1_ram_out), .Reset(Rst_Button_out), .Store(CPU_1_store), .R1(CPU_1_r1));
  LED L6 (.in(CPU_1_r0[6]));
  LED L7 (.in(CPU_1_r0[7]));
  LED LED_1 (.in(RAM_Addr[0]));
  LED LED_2 (.in(RAM_Addr[1]));
  LED LED_3 (.in(RAM_Addr[2]));
  LED LED_4 (.in(RAM_Addr[3]));
  LED LED_5 (.in(RAM_Addr[4]));
  LED LED_6 (.in(RAM_Addr[5]));
  LED LED_7 (.in(RAM_Addr[6]));
  LED LED_8 (.in(RAM_Addr[7]));
  Register #(.width(5)) register_1 (.D(adder_1_out), .clk(Clk), .Q(register_1_q), .clr(Rst));  // open: en
  Adder #(.width(5)) adder_1 (.a(5'b00001), .b(register_1_q), .out(adder_1_out));  // open: cin, cout
  Comparator #(.width(5)) comparator_1 (.a(adder_1_out), .b(5'b01011), .gt(Rst));  // open: eq, lt

  // Notes on the sheet:
  //   contents of ROMa (hex, n*v repeats v):
  //   b08c 2003 9008 2105 9104 9908 9a04 1889 9100 b00c
  //   Use only 8 bit adresses
  //   permet juste de reset après 10 instructions, pour tester et observer
  //   VCC 5V
  //   VCC 3.3V
  //   VCC 5V
  //   VCC 3.3V
  //   GROUND
  //   GROUND
  //   GROUND
  //   GROUND
endmodule

module CPU (
  input  [31:0] RAM_In,
  input  [15:0] ROM_In,
  input  Clk,
  input  Reset,
  output [31:0] R3,
  output [31:0] R4,
  output [31:0] R2,
  output [31:0] R5,
  output [31:0] R1,
  output [31:0] R6,
  output [31:0] R0,
  output [31:0] R7,
  output [7:0] ROM_Addr,
  output [31:0] RAM_Addr,
  output Store,
  output [31:0] RAM_Out
);

  wire Controller_1_carry, Controller_1_dp_shift, Controller_1_imm32_enable, Load;
  wire [2:0] Controller_1_rd, Controller_1_rm, Controller_1_rn;
  wire [3:0] Controller_1_alu_opcode, Flags;
  wire [4:0] A5, Controller_1_imm5, multiplexer_3_out;
  wire [31:0] ALU_In, Controller_1_imm32, multiplexer_1_out, multiplexer_2_out, Regs_1_bout;
  wire [31:5] AOut;

  Multiplexer #(.width(32), .enable("false")) multiplexer_1 (
    .in0(ALU_In), .in1(RAM_In), .out(multiplexer_1_out), .sel(Load));
  Controller Controller_1 (
    .Rm(Controller_1_rm), .ALU_Opcode(Controller_1_alu_opcode), .Rn(Controller_1_rn),
    .Imm32_Enable(Controller_1_imm32_enable), .Imm32(Controller_1_imm32), .Rd(Controller_1_rd),
    .Flags(Flags), .Imm5(Controller_1_imm5), .PC(ROM_Addr), .Inst(ROM_In), .DP_Shift(Controller_1_dp_shift),
    .Carry(Controller_1_carry), .RAM_Addr(RAM_Addr), .Load(Load), .Store(Store), .Clk(Clk), .Reset(Reset));
  BancRegistre Regs_1 (
    .DataIn(multiplexer_1_out), .BOut(Regs_1_bout), .AOut({AOut, A5}), .R0(R0), .R1(R1), .R2(R2), .R4(R4),
    .R5(R5), .R6(R6), .R7(R7), .RegDest(Controller_1_rd), .R3(R3), .RegA(Controller_1_rm),
    .RegB(Controller_1_rn), .Clk(Clk), .Reset(Reset));
  Multiplexer #(.width(32), .enable("false")) multiplexer_2 (
    .in0({AOut, A5}), .in1(Controller_1_imm32), .out(multiplexer_2_out), .sel(Controller_1_imm32_enable));
  Multiplexer #(.width(5), .enable("false")) multiplexer_3 (
    .in0(A5), .in1(Controller_1_imm5), .out(multiplexer_3_out), .sel(Controller_1_dp_shift));
  ALU ALU_1 (
    .S(ALU_In), .Flags(Flags), .A(multiplexer_2_out), .B(Regs_1_bout), .Shift(multiplexer_3_out),
    .CarryIn(Controller_1_carry), .Codop(Controller_1_alu_opcode));
  // Probe on ALU_In
  Pull_Resistor pull_resistor_1 (.node(RAM_Out));
  assign RAM_Out = Store ? {AOut, A5} : 32'bz;  // Controlled_Buffer controlled_buffer_1
  // Probe on Regs_1_bout
  // Probe on multiplexer_2_out

  // Other names for the same wires on the sheet: AOut[4:0] = A5
endmodule
