// Logisim project OldALU.circ as structural Verilog: 3 circuits, main circuit main
module main (
  input  [31:0] A,
  input  [31:0] B,
  input  [4:0] Shift,
  input  CarryIn,
  input  [3:0] Codop,
  output [31:0] S,
  output [3:0] Flags
);

  wire bitselector_2_out, bitselector_4_out, bitselector_5_out, C1, C2, C3, C4, C5, C6, C7,
       S_sign_different_out, Signs_equal_out;
  wire [4:0] negator_2_out, subtractor_3_out;
  wire [31:0] adder_1_out, adder_2_out, and_1_out, and_2_out, andnot_1_out_3, demultiplexer_1_out0,
       demultiplexer_1_out1, demultiplexer_1_out5, demultiplexer_1_out6, demultiplexer_1_out8,
       demultiplexer_1_out9, demultiplexer_1_out10, demultiplexer_1_out11, demultiplexer_1_out12,
       demultiplexer_1_out13, demultiplexer_1_out14, demultiplexer_2_out0, demultiplexer_2_out1,
       demultiplexer_2_out2, demultiplexer_2_out3, demultiplexer_2_out4, demultiplexer_2_out5,
       demultiplexer_2_out6, demultiplexer_2_out7, demultiplexer_2_out8, demultiplexer_2_out10,
       demultiplexer_2_out11, demultiplexer_2_out12, demultiplexer_2_out13, demultiplexer_2_out14,
       demultiplexer_2_out15, mult_32_1_out_3, negator_1_out, not_1_out, or_1_out, shifter_1_out,
       shifter_2_out, shifter_3_out, shifter_4_out, subtractor_1_out, subtractor_2_out, xor_1_out;

  Demultiplexer #(.select(4), .width(32), .enable("false")) demultiplexer_1 (
    .out0(demultiplexer_1_out0), .out1(demultiplexer_1_out1), .out5(demultiplexer_1_out5),
    .out6(demultiplexer_1_out6), .out8(demultiplexer_1_out8), .out9(demultiplexer_1_out9),
    .out10(demultiplexer_1_out10), .out11(demultiplexer_1_out11), .out12(demultiplexer_1_out12),
    .out13(demultiplexer_1_out13), .out14(demultiplexer_1_out14), .in(A), .sel(Codop));  // open: out2, out3, out4, out7, out15
  Demultiplexer #(.select(4), .width(32), .enable("false")) demultiplexer_2 (
    .out0(demultiplexer_2_out0), .out1(demultiplexer_2_out1), .out2(demultiplexer_2_out2),
    .out3(demultiplexer_2_out3), .out4(demultiplexer_2_out4), .out5(demultiplexer_2_out5),
    .out6(demultiplexer_2_out6), .out7(demultiplexer_2_out7), .out8(demultiplexer_2_out8),
    .out10(demultiplexer_2_out10), .out11(demultiplexer_2_out11), .out12(demultiplexer_2_out12),
    .out13(demultiplexer_2_out13), .out14(demultiplexer_2_out14), .out15(demultiplexer_2_out15), .in(B),
    .sel(Codop));  // open: out9
  assign and_1_out = demultiplexer_1_out0 & demultiplexer_2_out0;  // AND_Gate and_1, 32 bits wide
  assign xor_1_out = demultiplexer_1_out1 ^ demultiplexer_2_out1;  // XOR_Gate xor_1, 32 bits wide
  Shifter #(.width(32)) shifter_1 (.in(demultiplexer_2_out2), .\dist (Shift), .out(shifter_1_out));
  Shifter #(.width(32), .shift("lr")) shifter_2 (.in(demultiplexer_2_out3), .\dist (Shift), .out(shifter_2_out));
  Shifter #(.width(32), .shift("ar")) shifter_3 (.in(demultiplexer_2_out4), .\dist (Shift), .out(shifter_3_out));
  Adder #(.width(32)) adder_1 (
    .a(demultiplexer_1_out5), .b(demultiplexer_2_out5), .out(adder_1_out), .cin(CarryIn), .cout(C1));
  Shifter #(.width(32), .shift("rr")) shifter_4 (.in(demultiplexer_2_out7), .\dist (Shift), .out(shifter_4_out));
  Subtractor #(.width(32)) subtractor_1 (
    .a(demultiplexer_1_out6), .b(demultiplexer_2_out6), .out(subtractor_1_out), .bin(CarryIn), .bout(C2));
  assign and_2_out = demultiplexer_1_out8 & demultiplexer_2_out8;  // AND_Gate and_2, 32 bits wide
  Negator #(.width(32)) negator_1 (.in(demultiplexer_1_out9), .out(negator_1_out));
  Subtractor #(.width(32)) subtractor_2 (
    .a(demultiplexer_1_out10), .b(demultiplexer_2_out10), .out(subtractor_2_out), .bout(C3));  // open: bin
  Adder #(.width(32)) adder_2 (
    .a(demultiplexer_1_out11), .b(demultiplexer_2_out11), .out(adder_2_out), .cout(C4));  // open: cin
  assign or_1_out = demultiplexer_1_out12 | demultiplexer_2_out12;  // OR_Gate or_1, 32 bits wide
  mult_32 mult_32_1 (.in_1(demultiplexer_1_out13), .in_2(demultiplexer_2_out13), .out_3(mult_32_1_out_3));
  ANDNOT andnot_1 (.A(demultiplexer_1_out14), .B(demultiplexer_2_out14), .out_3(andnot_1_out_3));
  assign not_1_out = ~demultiplexer_2_out15;  // NOT_Gate not_1, 32 bits wide
  Multiplexer #(.select(4), .width(32), .enable("false")) multiplexer_1 (
    .in0(and_1_out), .in1(xor_1_out), .in2(shifter_1_out), .in3(shifter_2_out), .in4(shifter_3_out),
    .in5(adder_1_out), .in6(subtractor_1_out), .in7(shifter_4_out), .in8(and_2_out), .in9(negator_1_out),
    .in10(subtractor_2_out), .in11(adder_2_out), .in12(or_1_out), .in13(mult_32_1_out_3),
    .in14(andnot_1_out_3), .in15(not_1_out), .out(S), .sel(Codop));
  Negator #(.width(5)) negator_2 (.in(Shift), .out(negator_2_out));
  BitSelector #(.width(32)) bitselector_1 (.in(B), .out(C5), .sel(negator_2_out));
  Subtractor #(.width(5)) subtractor_3 (.a(Shift), .b(5'b00001), .out(subtractor_3_out));  // open: bin, bout
  Comparator #(.width(32)) comparator_1 (.a(S), .b({32{1'b0}}), .eq(Flags[2]), .lt(Flags[3]));  // open: gt
  Multiplexer #(.select(4), .enable("false")) multiplexer_2 (
    .in2(C5), .in3(C6), .in4(C6), .in5(C1), .in6(C2), .in7(C7), .in10(C3), .in11(C4), .out(Flags[1]),
    .sel(Codop));  // open: in0, in1, in8, in9, in12, in13, in14, in15
  BitSelector #(.width(32)) bitselector_2 (.in(B), .out(bitselector_2_out), .sel({5{1'b1}}));
  BitSelector #(.width(32)) bitselector_3 (.in(B), .out(C6), .sel(subtractor_3_out));
  BitSelector #(.width(32)) bitselector_4 (.in(A), .out(bitselector_4_out), .sel({5{1'b1}}));
  BitSelector #(.width(32)) bitselector_5 (.in(S), .out(bitselector_5_out), .sel({5{1'b1}}));
  BitSelector #(.width(32)) bitselector_6 (.in(S), .out(C7), .sel({5{1'b1}}));
  xnor Signs_equal (Signs_equal_out, bitselector_4_out, bitselector_2_out);
  xor S_sign_different (S_sign_different_out, bitselector_2_out, bitselector_5_out);
  and Overflow (Flags[0], Signs_equal_out, S_sign_different_out);
endmodule

module ANDNOT (
  input  [31:0] A,
  input  [31:0] B,
  output [31:0] out_3
);

  wire [31:0] not_1_out;

  assign out_3 = A & not_1_out;  // AND_Gate and_1, 32 bits wide
  assign not_1_out = ~B;  // NOT_Gate not_1, 32 bits wide
endmodule

module mult_32 (
  input  [31:0] in_1,
  input  [31:0] in_2,
  output [31:0] out_3
);

  wire [15:0] adder_1_out, bitselector_1_out, bitselector_2_out, bitselector_3_out, bitselector_4_out,
       multiplier_1_cout, multiplier_1_out, multiplier_2_out, multiplier_3_out;
  wire [31:0] bit_extender_1_out, bit_extender_2_out, shifter_1_out;

  BitSelector #(.width(32), .group(16)) bitselector_1 (.in(in_1), .out(bitselector_1_out), .sel(1'b0));
  BitSelector #(.width(32), .group(16)) bitselector_2 (.in(in_1), .out(bitselector_2_out), .sel(1'b1));
  BitSelector #(.width(32), .group(16)) bitselector_3 (.in(in_2), .out(bitselector_3_out), .sel(1'b0));
  BitSelector #(.width(32), .group(16)) bitselector_4 (.in(in_2), .out(bitselector_4_out), .sel(1'b1));
  Multiplier #(.width(16)) multiplier_1 (
    .a(bitselector_1_out), .b(bitselector_3_out), .out(multiplier_1_out), .cout(multiplier_1_cout));  // open: cin
  Multiplier #(.width(16)) multiplier_2 (
    .a(bitselector_1_out), .b(bitselector_4_out), .out(multiplier_2_out), .cin(multiplier_1_cout));  // open: cout
  Multiplier #(.width(16)) multiplier_3 (
    .a(bitselector_2_out), .b(bitselector_3_out), .out(multiplier_3_out));  // open: cin, cout
  assign bit_extender_1_out = {{16{multiplier_1_out[15]}}, multiplier_1_out};  // Bit_Extender bit_extender_1
  Adder #(.width(16)) adder_1 (.a(multiplier_2_out), .b(multiplier_3_out), .out(adder_1_out));  // open: cin, cout
  assign bit_extender_2_out = {{16{adder_1_out[15]}}, adder_1_out};  // Bit_Extender bit_extender_2
  Shifter #(.width(32)) shifter_1 (.in(bit_extender_2_out), .\dist (5'b10110), .out(shifter_1_out));
  assign out_3 = bit_extender_1_out | shifter_1_out;  // OR_Gate or_1, 32 bits wide
endmodule
