// Logisim project bancDeRegistre.circ as structural Verilog: 1 circuit, main circuit main
module main (
  input  [31:0] DataIn,
  input  [2:0] RegA,
  input  [2:0] RegDest,
  input  [2:0] RegB,
  input  in_5,
  output [31:0] Aout,
  output [31:0] Bout
);

  wire clock_1_out, demultiplexer_1_out0, demultiplexer_1_out1, demultiplexer_1_out2, demultiplexer_1_out3,
       demultiplexer_1_out4, demultiplexer_1_out5, demultiplexer_1_out6, demultiplexer_1_out7;
  wire [31:0] DataOut0, DataOut1, DataOut2, DataOut3, DataOut4, DataOut5, DataOut6, DataOut7;

  Clock clock_1 (.out(clock_1_out));
  Demultiplexer #(.select(3)) demultiplexer_1 (
    .out0(demultiplexer_1_out0), .out1(demultiplexer_1_out1), .out2(demultiplexer_1_out2),
    .out3(demultiplexer_1_out3), .out4(demultiplexer_1_out4), .out5(demultiplexer_1_out5),
    .out6(demultiplexer_1_out6), .out7(demultiplexer_1_out7), .in(clock_1_out), .sel(RegDest));  // open: en
  Register #(.width(32)) R0 (.D(DataIn), .clk(demultiplexer_1_out0), .Q(DataOut0), .clr(in_5));  // open: en
  Register #(.width(32)) R1 (.D(DataIn), .clk(demultiplexer_1_out1), .Q(DataOut1), .clr(in_5));  // open: en
  Register #(.width(32)) R7 (.D(DataIn), .clk(demultiplexer_1_out2), .Q(DataOut2), .clr(in_5));  // open: en
  Register #(.width(32)) R3 (.D(DataIn), .clk(demultiplexer_1_out3), .Q(DataOut3), .clr(in_5));  // open: en
  Register #(.width(32)) R4 (.D(DataIn), .clk(demultiplexer_1_out4), .Q(DataOut4), .clr(in_5));  // open: en
  Register #(.width(32)) R5 (.D(DataIn), .clk(demultiplexer_1_out5), .Q(DataOut5), .clr(in_5));  // open: en
  Register #(.width(32)) R6 (.D(DataIn), .clk(demultiplexer_1_out6), .Q(DataOut6), .clr(in_5));  // open: en
  Register #(.width(32)) R7_2 (.D(DataIn), .clk(demultiplexer_1_out7), .Q(DataOut7), .clr(in_5));  // open: en
  Multiplexer #(.select(3), .width(32)) multiplexer_1 (
    .in0(DataOut0), .in1(DataOut1), .in2(DataOut2), .in3(DataOut3), .in4(DataOut4), .in5(DataOut5),
    .in6(DataOut6), .in7(DataOut7), .out(Aout), .sel(RegA));  // open: en
  Multiplexer #(.select(3), .width(32)) multiplexer_2 (
    .in0(DataOut0), .in1(DataOut1), .in2(DataOut2), .in3(DataOut3), .in4(DataOut4), .in5(DataOut5),
    .in6(DataOut6), .in7(DataOut7), .out(Bout), .sel(RegB));  // open: en
endmodule
